// Logisim project logic_schematic.circ as structural Verilog: 2 circuits, main circuit main
module main (
  input  [15:0] in_1,
  input  [15:0] in_2,
  input  [6:0] in_3,
  input  [6:0] in_4
);

  wire [15:0] adder_1_out, alu_1_a_out, alu_1_b_out, alu_1_q1_out, alu_1_q2_out, subtractor_1_out;

  ALU alu_1 (
    .A_Out(alu_1_a_out), .B_Out(alu_1_b_out), .Q1_Out(alu_1_q1_out), .Q2_Out(alu_1_q2_out), .Q2_Sel(in_3),
    .Q1_Sel(in_4), .op2(adder_1_out), .op3(subtractor_1_out), .A_In(in_2), .B_In(in_1));  // open: op4, op5, op6, op7
  // Probe on alu_1_q2_out
  // Probe on alu_1_q1_out
  Adder #(.width(16)) adder_1 (.a(alu_1_b_out), .b(alu_1_a_out), .out(adder_1_out));  // open: cin, cout
  Subtractor #(.width(16)) subtractor_1 (.a(alu_1_b_out), .b(alu_1_a_out), .out(subtractor_1_out));  // open: bin, bout
endmodule

module ALU (
  input  [6:0] Q1_Sel,
  input  [15:0] A_In,
  input  [15:0] B_In,
  input  [15:0] op2,
  input  [15:0] op3,
  input  [15:0] op4,
  input  [15:0] op5,
  input  [15:0] op6,
  input  [15:0] op7,
  input  [6:0] Q2_Sel,
  output [15:0] A_Out,
  output [15:0] B_Out,
  output [15:0] Q1_Out,
  output [15:0] Q2_Out
);

  wire decoder_1_out0, decoder_1_out1, decoder_1_out2, decoder_1_out3, decoder_1_out4, decoder_1_out5,
       decoder_1_out6, decoder_1_out7, decoder_2_out0, decoder_2_out1, decoder_2_out2, decoder_2_out3,
       decoder_2_out4, decoder_2_out5, decoder_2_out6, decoder_2_out7, nor_1_out, nor_2_out;
  wire [3:0] xor_1_out, xor_2_out;

  assign xor_1_out = 4'b0001 ^ Q1_Sel[6:3];  // XOR_Gate xor_1, 4 bits wide
  assign xor_2_out = Q2_Sel[6:3] ^ 4'b0001;  // XOR_Gate xor_2, 4 bits wide
  nor nor_1 (nor_1_out, xor_1_out[0], xor_1_out[1], xor_1_out[2], xor_1_out[3]);
  nor nor_2 (nor_2_out, xor_2_out[0], xor_2_out[1], xor_2_out[2], xor_2_out[3]);
  Decoder #(.select(3)) decoder_1 (
    .out0(decoder_1_out0), .out1(decoder_1_out1), .out2(decoder_1_out2), .out3(decoder_1_out3),
    .out4(decoder_1_out4), .out5(decoder_1_out5), .out6(decoder_1_out6), .out7(decoder_1_out7),
    .sel(Q1_Sel[2:0]), .en(nor_1_out));
  assign Q1_Out = decoder_1_out0 ? A_In : 16'bz;  // Controlled_Buffer controlled_buffer_1
  assign Q1_Out = decoder_1_out1 ? B_In : 16'bz;  // Controlled_Buffer controlled_buffer_2
  assign Q1_Out = decoder_1_out2 ? op2 : 16'bz;  // Controlled_Buffer controlled_buffer_3
  assign Q2_Out = decoder_2_out2 ? op2 : 16'bz;  // Controlled_Buffer controlled_buffer_4
  assign Q2_Out = decoder_2_out1 ? B_In : 16'bz;  // Controlled_Buffer controlled_buffer_5
  assign Q2_Out = decoder_2_out0 ? A_In : 16'bz;  // Controlled_Buffer controlled_buffer_6
  Decoder #(.select(3)) decoder_2 (
    .out0(decoder_2_out0), .out1(decoder_2_out1), .out2(decoder_2_out2), .out3(decoder_2_out3),
    .out4(decoder_2_out4), .out5(decoder_2_out5), .out6(decoder_2_out6), .out7(decoder_2_out7),
    .sel(Q2_Sel[2:0]), .en(nor_2_out));
  assign Q1_Out = decoder_1_out3 ? op3 : 16'bz;  // Controlled_Buffer controlled_buffer_7
  assign Q1_Out = decoder_1_out4 ? op4 : 16'bz;  // Controlled_Buffer controlled_buffer_8
  assign Q1_Out = decoder_1_out5 ? op5 : 16'bz;  // Controlled_Buffer controlled_buffer_9
  assign Q1_Out = decoder_1_out6 ? op6 : 16'bz;  // Controlled_Buffer controlled_buffer_10
  assign Q1_Out = decoder_1_out7 ? op7 : 16'bz;  // Controlled_Buffer controlled_buffer_11
  assign Q2_Out = decoder_2_out7 ? op7 : 16'bz;  // Controlled_Buffer controlled_buffer_12
  assign Q2_Out = decoder_2_out6 ? op6 : 16'bz;  // Controlled_Buffer controlled_buffer_13
  assign Q2_Out = decoder_2_out5 ? op5 : 16'bz;  // Controlled_Buffer controlled_buffer_14
  assign Q2_Out = decoder_2_out4 ? op4 : 16'bz;  // Controlled_Buffer controlled_buffer_15
  assign Q2_Out = decoder_2_out3 ? op3 : 16'bz;  // Controlled_Buffer controlled_buffer_16

  assign A_Out = A_In;
  assign B_Out = B_In;
endmodule
