// Logisim project Activation_Module.circ as structural Verilog: 2 circuits, main circuit main
module main (
  input  [15:0] in_1,
  input  [6:0] in_2,
  input  [6:0] in_3,
  input  [6:0] in_4,
  input  [6:0] in_5
);

  wire activationmodule_1_p10, activationmodule_1_p11, activationmodule_1_p12, activationmodule_1_p15,
       activationmodule_1_p16, and_1_out, and_2_out, clock_1_out, not_1_out, not_2_out, not_3_out;
  wire [6:0] dipswitch_1_sw7, dipswitch_2_sw7;
  wire [15:0] activationmodule_1_p13, activationmodule_1_p14, register_1_q;

  not not_1 (not_1_out, clock_1_out);
  Clock clock_1 (.out(clock_1_out));
  and and_1 (and_1_out, not_1_out, not_2_out);
  not not_2 (not_2_out, not_1_out);
  and and_2 (and_2_out, clock_1_out, not_3_out);
  not not_3 (not_3_out, clock_1_out);
  DipSwitch #(.number(7)) dipswitch_1 (
    .sw1(dipswitch_1_sw7[6]), .sw2(dipswitch_1_sw7[5]), .sw3(dipswitch_1_sw7[4]), .sw4(dipswitch_1_sw7[3]),
    .sw5(dipswitch_1_sw7[2]), .sw6(dipswitch_1_sw7[1]), .sw7(dipswitch_1_sw7[0]));
  DipSwitch #(.number(7)) dipswitch_2 (
    .sw1(dipswitch_2_sw7[6]), .sw2(dipswitch_2_sw7[5]), .sw3(dipswitch_2_sw7[4]), .sw4(dipswitch_2_sw7[3]),
    .sw5(dipswitch_2_sw7[2]), .sw6(dipswitch_2_sw7[1]), .sw7(dipswitch_2_sw7[0]));
  // Probe on activationmodule_1_p12
  // Probe on activationmodule_1_p10
  // ActivationModule activationmodule_1: pin names not known; wires that end beside it: and_1_out, and_2_out, in_2, in_3, in_4, in_5, dipswitch_1_sw7, dipswitch_2_sw7, in_1, activationmodule_1_p10, activationmodule_1_p11, activationmodule_1_p12, activationmodule_1_p13, activationmodule_1_p14, activationmodule_1_p15, activationmodule_1_p16
  Register #(.trigger("high"), .width(16)) register_1 (
    .D(activationmodule_1_p14), .clk(activationmodule_1_p15), .Q(register_1_q));  // open: en, clr
  Register #(.trigger("high"), .width(16)) register_2 (
    .D(register_1_q), .clk(activationmodule_1_p16), .Q(activationmodule_1_p13));  // open: en, clr
  // Probe on activationmodule_1_p13
endmodule

module ActivationModule (
  input  [3:0] PatternR,
  input  [6:0] RE1,
  input  [15:0] To_Bus,
  input  [6:0] RE2,
  input  [15:0] BUS1_In,
  input  [15:0] BUS2_In,
  input  [3:0] PatternW,
  input  CLK_F,
  input  [6:0] WE1,
  input  CLK_R,
  input  [6:0] WE2,
  output [2:0] Mode_R,
  output RE,
  output [15:0] BUS1_Out,
  output [15:0] BUS2_Out,
  output [2:0] Mode_W,
  output [15:0] from_Bus,
  output WE_F,
  output WE_R
);

  wire not_1_out, not_2_out, not_3_out, not_4_out, or_1_out, or_2_out, or_3_out, or_4_out, or_5_out,
       or_6_out, or_7_out, or_8_out, or_9_out, or_10_out, or_11_out, or_12_out, xor_6_out;
  wire [3:0] xor_1_out, xor_2_out, xor_3_out, xor_4_out;

  assign Mode_R = not_1_out ? RE1[2:0] : 3'bz;  // Controlled_Buffer controlled_buffer_1
  assign Mode_R = or_9_out ? RE2[2:0] : 3'bz;  // Controlled_Buffer controlled_buffer_2
  assign Mode_W = not_2_out ? WE1[2:0] : 3'bz;  // Controlled_Buffer controlled_buffer_3
  assign Mode_W = or_11_out ? WE2[2:0] : 3'bz;  // Controlled_Buffer controlled_buffer_4
  not not_1 (not_1_out, or_9_out);
  assign xor_1_out = PatternR ^ RE1[6:3];  // XOR_Gate xor_1, 4 bits wide
  assign xor_2_out = PatternR ^ RE2[6:3];  // XOR_Gate xor_2, 4 bits wide
  not not_2 (not_2_out, or_11_out);
  assign xor_3_out = PatternW ^ WE1[6:3];  // XOR_Gate xor_3, 4 bits wide
  assign xor_4_out = PatternW ^ WE2[6:3];  // XOR_Gate xor_4, 4 bits wide
  or or_1 (or_1_out, xor_1_out[1], or_2_out);
  or or_2 (or_2_out, xor_1_out[2], xor_1_out[3]);
  or or_3 (or_3_out, xor_2_out[1], or_4_out);
  or or_4 (or_4_out, xor_2_out[2], xor_2_out[3]);
  or or_5 (or_5_out, xor_3_out[1], or_6_out);
  or or_6 (or_6_out, xor_3_out[2], xor_3_out[3]);
  or or_7 (or_7_out, xor_4_out[1], or_8_out);
  or or_8 (or_8_out, xor_4_out[2], xor_4_out[3]);
  or or_9 (or_9_out, xor_1_out[0], or_1_out);
  or or_10 (or_10_out, xor_2_out[0], or_3_out);
  or or_11 (or_11_out, xor_3_out[0], or_5_out);
  or or_12 (or_12_out, xor_4_out[0], or_7_out);
  xor xor_5 (RE, or_9_out, or_10_out);
  not not_3 (not_3_out, RE);
  xor xor_6 (xor_6_out, or_11_out, or_12_out);
  not not_4 (not_4_out, xor_6_out);
  and and_1 (WE_F, xor_6_out, CLK_F);
  and and_2 (WE_R, xor_6_out, CLK_R);
  assign BUS1_Out = RE ? To_Bus : 16'bz;  // Controlled_Buffer controlled_buffer_5
  assign BUS2_Out = not_3_out ? To_Bus : 16'bz;  // Controlled_Buffer controlled_buffer_6
  assign from_Bus = xor_6_out ? BUS1_In : 16'bz;  // Controlled_Buffer controlled_buffer_7
  assign from_Bus = not_4_out ? BUS2_In : 16'bz;  // Controlled_Buffer controlled_buffer_8
endmodule
