// Logisim project Activation_Module.circ as structural Verilog: 2 circuits, main circuit main
module main (
  input  [15:0] in_1,
  input  [6:0] in_2,
  input  [6:0] in_3,
  input  [6:0] in_4,
  input  [6:0] in_5
);

  wire activationmodule_1_we_f, activationmodule_1_we_r, and_1_out, and_2_out, clock_1_out, not_1_out,
       not_2_out, not_3_out;
  wire [3:0] dipswitch_1_sw4, dipswitch_2_sw4;
  wire [15:0] activationmodule_1_bus1_out, activationmodule_1_bus2_out, activationmodule_1_from_bus,
       register_1_q, register_2_q, undriven;

  not not_1 (not_1_out, clock_1_out);
  Clock clock_1 (.out(clock_1_out));
  and and_1 (and_1_out, not_1_out, not_2_out);
  not not_2 (not_2_out, not_1_out);
  and and_2 (and_2_out, clock_1_out, not_3_out);
  not not_3 (not_3_out, clock_1_out);
  DipSwitch #(.number(4)) dipswitch_1 (
    .sw1(dipswitch_1_sw4[3]), .sw2(dipswitch_1_sw4[2]), .sw3(dipswitch_1_sw4[1]), .sw4(dipswitch_1_sw4[0]));
  DipSwitch #(.number(4)) dipswitch_2 (
    .sw1(dipswitch_2_sw4[3]), .sw2(dipswitch_2_sw4[2]), .sw3(dipswitch_2_sw4[1]), .sw4(dipswitch_2_sw4[0]));
  // Probe on activationmodule_1_bus2_out
  // Probe on activationmodule_1_bus1_out
  ActivationModule activationmodule_1 (
    .WE_F(activationmodule_1_we_f), .WE_R(activationmodule_1_we_r), .from_Bus(activationmodule_1_from_bus),
    .BUS1_Out(activationmodule_1_bus1_out), .BUS2_Out(activationmodule_1_bus2_out), .RE1(in_2), .RE2(in_3),
    .WE1(in_4), .WE2(in_5), .PatternR(dipswitch_1_sw4), .PatternW(dipswitch_2_sw4), .CLK_F(and_1_out),
    .CLK_R(and_2_out), .To_Bus(register_2_q), .BUS1_In(in_1), .BUS2_In(undriven));  // open: Mode_W, Mode_R, RE
  Register #(.trigger("high"), .width(16)) register_1 (
    .D(activationmodule_1_from_bus), .clk(activationmodule_1_we_r), .Q(register_1_q));  // open: en, clr
  Register #(.trigger("high"), .width(16)) register_2 (
    .D(register_1_q), .clk(activationmodule_1_we_f), .Q(register_2_q));  // open: en, clr
  // Probe on register_2_q
endmodule

module ActivationModule (
  input  [3:0] PatternR,
  input  [6:0] RE1,
  input  [15:0] To_Bus,
  input  [6:0] RE2,
  input  [15:0] BUS1_In,
  input  [15:0] BUS2_In,
  input  [3:0] PatternW,
  input  [6:0] WE1,
  input  CLK_F,
  input  [6:0] WE2,
  input  CLK_R,
  output [2:0] Mode_R,
  output RE,
  output [15:0] BUS1_Out,
  output [15:0] BUS2_Out,
  output [2:0] Mode_W,
  output [15:0] from_Bus,
  output WE_F,
  output WE_R
);

  wire not_1_out, not_2_out, or_1_out, or_2_out, or_3_out, or_4_out, or_5_out, or_6_out, or_7_out, or_8_out,
       or_9_out, or_10_out, or_11_out, or_12_out, xor_5_out;
  wire [3:0] xor_1_out, xor_2_out, xor_3_out, xor_4_out;

  assign Mode_R = not_1_out ? RE1[2:0] : 3'bz;  // Controlled_Buffer controlled_buffer_1
  assign Mode_R = or_9_out ? RE2[2:0] : 3'bz;  // Controlled_Buffer controlled_buffer_2
  assign Mode_W = not_2_out ? WE1[2:0] : 3'bz;  // Controlled_Buffer controlled_buffer_3
  assign Mode_W = or_11_out ? WE2[2:0] : 3'bz;  // Controlled_Buffer controlled_buffer_4
  not not_1 (not_1_out, or_9_out);
  assign xor_1_out = PatternR ^ RE1[6:3];  // XOR_Gate xor_1, 4 bits wide
  assign xor_2_out = PatternR ^ RE2[6:3];  // XOR_Gate xor_2, 4 bits wide
  not not_2 (not_2_out, or_11_out);
  assign xor_3_out = PatternW ^ WE1[6:3];  // XOR_Gate xor_3, 4 bits wide
  assign xor_4_out = PatternW ^ WE2[6:3];  // XOR_Gate xor_4, 4 bits wide
  or or_1 (or_1_out, xor_1_out[1], or_2_out);
  or or_2 (or_2_out, xor_1_out[2], xor_1_out[3]);
  or or_3 (or_3_out, xor_2_out[1], or_4_out);
  or or_4 (or_4_out, xor_2_out[2], xor_2_out[3]);
  or or_5 (or_5_out, xor_3_out[1], or_6_out);
  or or_6 (or_6_out, xor_3_out[2], xor_3_out[3]);
  or or_7 (or_7_out, xor_4_out[1], or_8_out);
  or or_8 (or_8_out, xor_4_out[2], xor_4_out[3]);
  or or_9 (or_9_out, xor_1_out[0], or_1_out);
  or or_10 (or_10_out, xor_2_out[0], or_3_out);
  or or_11 (or_11_out, xor_3_out[0], or_5_out);
  or or_12 (or_12_out, xor_4_out[0], or_7_out);
  xor xor_5 (xor_5_out, or_11_out, or_12_out);
  xor xor_6 (RE, or_9_out, or_10_out);
  and and_1 (WE_F, xor_5_out, CLK_F);
  and and_2 (WE_R, xor_5_out, CLK_R);
  assign BUS1_Out = or_9_out ? To_Bus : 16'bz;  // Controlled_Buffer controlled_buffer_5
  assign BUS2_Out = or_10_out ? To_Bus : 16'bz;  // Controlled_Buffer controlled_buffer_6
  assign from_Bus = or_11_out ? BUS1_In : 16'bz;  // Controlled_Buffer controlled_buffer_7
  assign from_Bus = or_12_out ? BUS2_In : 16'bz;  // Controlled_Buffer controlled_buffer_8
endmodule
