// Logisim project Dual_Register.circ as structural Verilog
module Dual_Register (
  input  [15:0] Data_In,
  input  CLK_R,
  input  WE_F,
  input  Sup,
  input  HL,
  output [15:0] D_H_Out,
  output [15:0] D_L_Out
);

  wire and_1_out, and_2_out, and_3_out, not_1_out;
  wire [15:0] register_1_q;

  not not_1 (not_1_out, HL);
  Register #(.trigger("high"), .width(16)) register_1 (
    .D(Data_In), .en(CLK_R), .clk(CLK_R), .Q(register_1_q));  // open: clr
  and and_1 (and_1_out, WE_F, Sup);
  and and_2 (and_2_out, and_1_out, HL);
  and and_3 (and_3_out, and_1_out, not_1_out);
  Register #(.trigger("high"), .width(16)) register_2 (
    .D(register_1_q), .en(and_3_out), .clk(and_3_out), .Q(D_H_Out));  // open: clr
  Register #(.trigger("high"), .width(16)) register_3 (
    .D(register_1_q), .en(and_2_out), .clk(and_2_out), .Q(D_L_Out));  // open: clr
endmodule
