// Logisim project Instruction_Decoder.circ as structural Verilog
module Instruction_Decoder (
  input  [15:0] Ins_L_In,
  input  [15:0] Ins_H_In,
  input  CLK_R,
  input  CLK_F,
  output Const_Reg,
  output [2:0] Reg_Sel_In,
  output [2:0] Reg_Sel_A,
  output [2:0] Reg_Sel_B,
  output [15:0] Const_Out,
  output [6:0] WE1_Out,
  output [6:0] WE2_Out,
  output [6:0] RE1_Out,
  output [6:0] RE2_Out
);

  wire [1:0] adder_1_out, register_2_q;
  wire [5:0] register_2_q_2;
  wire [7:0] register_1_q;

  Adder #(.width(2)) adder_1 (.a(2'b01), .b(register_2_q), .out(adder_1_out));  // open: cin, cout
  Register #(.trigger("high")) register_1 (
    .D({Ins_L_In[5:0], adder_1_out}), .clk(CLK_R), .Q(register_1_q));  // open: en, clr
  Register #(.trigger("high")) register_2 (
    .D(register_1_q), .clk(CLK_F), .Q({register_2_q_2, register_2_q}));  // open: en, clr
  ROM #(.dataWidth(7), .misaligned("true")) rom_1 (.addr({register_2_q_2, register_2_q}), .data(WE1_Out));
  ROM #(.dataWidth(7), .misaligned("true")) rom_2 (.addr({register_2_q_2, register_2_q}), .data(WE2_Out));
  ROM #(.dataWidth(7), .misaligned("true")) rom_3 (.addr({register_2_q_2, register_2_q}), .data(RE1_Out));
  ROM #(.dataWidth(7), .misaligned("true")) rom_4 (.addr({register_2_q_2, register_2_q}), .data(RE2_Out));

  assign Const_Out = Ins_H_In;
  assign Const_Reg = Ins_L_In[6];
  assign Reg_Sel_A = Ins_L_In[12:10];
  assign Reg_Sel_B = Ins_L_In[15:13];
  assign Reg_Sel_In = Ins_L_In[9:7];
endmodule
