// Logisim project Interrupt_Controller.circ as structural Verilog: 2 circuits, main circuit main_Interrupt_Controller
module main_Interrupt_Controller (
  input  in_1,
  input  in_2,
  input  in_3,
  input  in_4,
  input  [15:0] in_5,
  input  in_6
);

  wire and_1_out, and_2_out, clock_1_out, interrupt_controller_1_s_sup, not_1_out, not_2_out, not_3_out;
  wire [15:0] interrupt_controller_1_ip_out;

  Clock clock_1 (.out(clock_1_out));
  not not_1 (not_1_out, clock_1_out);
  not not_2 (not_2_out, not_3_out);
  not not_3 (not_3_out, clock_1_out);
  and and_1 (and_1_out, not_1_out, clock_1_out);
  Interrupt_Controller interrupt_controller_1 (
    .IP_Out(interrupt_controller_1_ip_out), .S_Sup(interrupt_controller_1_s_sup), .CLK_R(and_1_out),
    .CLK_F(and_2_out), .RE(in_6), .IO_Int_In(in_3), .S_Int(in_4), .T2_Int_In(in_1), .T1_Int_In(in_2),
    .IV_OINT_In(16'h4), .IV_IO_In(16'h3), .IV_T1_In(16'h2), .IV_T2_In(16'h1), .IP_In({16{1'b0}}),
    .FLAG_In(in_5));
  and and_2 (and_2_out, not_2_out, not_3_out);
  // Probe on interrupt_controller_1_s_sup
  // Probe on interrupt_controller_1_ip_out
endmodule

module Interrupt_Controller (
  input  T2_Int_In,
  input  T1_Int_In,
  input  IO_Int_In,
  input  S_Int,
  input  CLK_R,
  input  CLK_F,
  input  [15:0] FLAG_In,
  input  RE,
  input  [15:0] IV_OINT_In,
  input  [15:0] IV_IO_In,
  input  [15:0] IV_T1_In,
  input  [15:0] IV_T2_In,
  input  [15:0] IP_In,
  output S_Sup,
  output [15:0] IP_Out
);

  wire and_1_out, and_2_out, and_4_out, and_5_out, and_6_out, and_7_out, and_8_out, and_9_out, and_10_out,
       and_11_out, and_12_out, d_ff_1_q, d_ff_2_q, d_ff_3_q, d_ff_4_q, d_ff_5_q, d_ff_6_q, d_ff_7_q,
       d_ff_8_q, j_k_ff_1_q, j_k_ff_2_q, j_k_ff_3_q, j_k_ff_4_q, not_1_out, not_2_out, not_3_out, not_4_out,
       not_5_out, not_6_out, not_7_out, or_1_out, or_2_out, or_3_out;

  and and_1 (and_1_out, RE, or_2_out);
  J_K_Flip_Flop j_k_ff_1 (.Q(j_k_ff_1_q), .preset(S_Int), .reset(d_ff_1_q));  // open: J, K, clk, Qn
  D_Flip_Flop d_ff_1 (.D(d_ff_2_q), .clk(CLK_R), .Q(d_ff_1_q));  // open: Qn, preset, reset
  D_Flip_Flop d_ff_2 (.D(j_k_ff_1_q), .clk(and_2_out), .Q(d_ff_2_q));  // open: Qn, preset, reset
  and and_2 (and_2_out, CLK_F, RE);
  and and_3 (S_Sup, CLK_R, and_1_out);
  or or_1 (or_1_out, j_k_ff_1_q, and_5_out);
  or or_2 (or_2_out, or_1_out, or_3_out);
  or or_3 (or_3_out, and_7_out, and_9_out);
  not not_1 (not_1_out, or_2_out);
  J_K_Flip_Flop j_k_ff_2 (.Q(j_k_ff_2_q), .preset(IO_Int_In), .reset(d_ff_3_q));  // open: J, K, clk, Qn
  D_Flip_Flop d_ff_3 (.D(d_ff_4_q), .clk(CLK_R), .Q(d_ff_3_q));  // open: Qn, preset, reset
  D_Flip_Flop d_ff_4 (.D(and_5_out), .clk(and_2_out), .Q(d_ff_4_q));  // open: Qn, preset, reset
  not not_2 (not_2_out, j_k_ff_1_q);
  assign IP_Out = j_k_ff_1_q ? IV_OINT_In : 16'bz;  // Controlled_Buffer controlled_buffer_1
  and and_4 (and_4_out, j_k_ff_2_q, not_7_out);
  and and_5 (and_5_out, not_2_out, and_4_out);
  assign IP_Out = and_5_out ? IV_IO_In : 16'bz;  // Controlled_Buffer controlled_buffer_2
  J_K_Flip_Flop j_k_ff_3 (.Q(j_k_ff_3_q), .preset(T1_Int_In), .reset(d_ff_5_q));  // open: J, K, clk, Qn
  D_Flip_Flop d_ff_5 (.D(d_ff_6_q), .clk(CLK_R), .Q(d_ff_5_q));  // open: Qn, preset, reset
  D_Flip_Flop d_ff_6 (.D(and_7_out), .clk(and_2_out), .Q(d_ff_6_q));  // open: Qn, preset, reset
  and and_6 (and_6_out, not_2_out, and_8_out);
  not not_3 (not_3_out, and_5_out);
  and and_7 (and_7_out, not_3_out, and_6_out);
  assign IP_Out = and_7_out ? IV_T1_In : 16'bz;  // Controlled_Buffer controlled_buffer_3
  J_K_Flip_Flop j_k_ff_4 (.Q(j_k_ff_4_q), .preset(T2_Int_In), .reset(d_ff_7_q));  // open: J, K, clk, Qn
  D_Flip_Flop d_ff_7 (.D(d_ff_8_q), .clk(CLK_R), .Q(d_ff_7_q));  // open: Qn, preset, reset
  D_Flip_Flop d_ff_8 (.D(and_9_out), .clk(and_2_out), .Q(d_ff_8_q));  // open: Qn, preset, reset
  and and_8 (and_8_out, j_k_ff_3_q, not_5_out);
  not not_4 (not_4_out, and_7_out);
  and and_9 (and_9_out, not_4_out, and_12_out);
  not not_5 (not_5_out, FLAG_In[8]);
  not not_6 (not_6_out, FLAG_In[9]);
  not not_7 (not_7_out, FLAG_In[10]);
  and and_10 (and_10_out, j_k_ff_4_q, not_6_out);
  and and_11 (and_11_out, not_2_out, and_10_out);
  and and_12 (and_12_out, not_3_out, and_11_out);
  assign IP_Out = and_9_out ? IV_T2_In : 16'bz;  // Controlled_Buffer controlled_buffer_4
  assign IP_Out = not_1_out ? IP_In : 16'bz;  // Controlled_Buffer controlled_buffer_5
endmodule
