// Logisim project logic_schematic.circ as structural Verilog
module Interrupt_Controller (
  input  T2_Int_In,
  input  T1_Int_In,
  input  IO_Int_In,
  input  S_Int,
  input  [15:0] FLAG_In,
  input  CLK_F,
  input  RE,
  input  CLK_R,
  input  [15:0] IV_OINT_In,
  input  [15:0] IV_IO_In,
  input  [15:0] IV_T1_In,
  input  [15:0] IV_T2_In,
  input  [15:0] IP_In,
  output S_Sup,
  output [15:0] IP_Out
);

  wire and_1_out, and_3_out, and_4_out, and_5_out, and_6_out, and_7_out, and_8_out, and_9_out, and_10_out,
       and_11_out, and_12_out, and_13_out, and_14_out, and_15_out, d_ff_1_q, j_k_ff_1_q, j_k_ff_2_q,
       j_k_ff_3_q, j_k_ff_4_q, not_1_out, not_2_out, not_3_out, not_4_out, not_5_out, not_6_out, not_7_out,
       or_1_out, or_2_out, or_3_out, undriven;

  D_Flip_Flop d_ff_1 (.D(RE), .clk(CLK_R), .Q(d_ff_1_q));  // open: Qn, preset, reset
  buf and_1 (and_1_out, d_ff_1_q);  // AND_Gate
  and and_2 (S_Sup, CLK_R, or_2_out);
  J_K_Flip_Flop j_k_ff_1 (.Q(j_k_ff_1_q), .preset(S_Int), .reset(and_3_out));  // open: J, K, clk, Qn
  and and_3 (and_3_out, undriven, and_1_out);
  J_K_Flip_Flop j_k_ff_2 (.Q(j_k_ff_2_q), .preset(IO_Int_In), .reset(and_4_out));  // open: J, K, clk, Qn
  assign IP_Out = j_k_ff_1_q ? IV_OINT_In : 16'bz;  // Controlled_Buffer controlled_buffer_1
  and and_4 (and_4_out, undriven, and_5_out);
  and and_5 (and_5_out, and_1_out, and_7_out);
  and and_6 (and_6_out, j_k_ff_2_q, not_5_out);
  and and_7 (and_7_out, and_6_out, not_1_out);
  J_K_Flip_Flop j_k_ff_3 (.Q(j_k_ff_3_q), .preset(T1_Int_In), .reset(and_8_out));  // open: J, K, clk, Qn
  and and_8 (and_8_out, undriven, and_9_out);
  and and_9 (and_9_out, and_1_out, and_13_out);
  not not_1 (not_1_out, j_k_ff_1_q);
  assign IP_Out = and_7_out ? IV_IO_In : 16'bz;  // Controlled_Buffer controlled_buffer_2
  J_K_Flip_Flop j_k_ff_4 (.Q(j_k_ff_4_q), .preset(T2_Int_In), .reset(and_10_out));  // open: J, K, clk, Qn
  and and_10 (and_10_out, undriven, and_11_out);
  and and_11 (and_11_out, and_1_out, and_15_out);
  and and_12 (and_12_out, j_k_ff_3_q, not_3_out);
  or or_1 (or_1_out, j_k_ff_1_q, and_6_out);
  not not_2 (not_2_out, or_1_out);
  and and_13 (and_13_out, and_12_out, not_2_out);
  assign IP_Out = and_13_out ? IV_T1_In : 16'bz;  // Controlled_Buffer controlled_buffer_3
  not not_3 (not_3_out, FLAG_In[8]);
  not not_4 (not_4_out, FLAG_In[9]);
  not not_5 (not_5_out, FLAG_In[10]);
  and and_14 (and_14_out, j_k_ff_4_q, not_4_out);
  or or_2 (or_2_out, or_1_out, and_12_out);
  not not_6 (not_6_out, or_2_out);
  or or_3 (or_3_out, or_2_out, and_14_out);
  and and_15 (and_15_out, and_14_out, not_6_out);
  not not_7 (not_7_out, or_3_out);
  assign IP_Out = and_15_out ? IV_T2_In : 16'bz;  // Controlled_Buffer controlled_buffer_4
  assign IP_Out = not_7_out ? IP_In : 16'bz;  // Controlled_Buffer controlled_buffer_5
endmodule
