// Logisim project Memory_Controller.circ as structural Verilog: 5 circuits, main circuit main_Memory
module main_Memory (
  input  [15:0] Addr_In,
  input  [15:0] Data_In,
  input  WE,
  input  RE,
  input  SUP
);

  wire and_1_out, and_2_out, and_3_out, bank_controller_1_oe_out, bank_controller_1_we_out,
       bank_module_x2_1_oe_out, bank_module_x2_1_we_out, bank_module_x2_2_oe_out, bank_module_x2_2_we_out,
       bank_module_x2_3_oe_out, bank_module_x2_3_we_out, bank_module_x4_1_oe_out, bank_module_x4_1_we_out,
       clock_1_out, memory_1_re_out, memory_1_we_f_out, not_1_out, not_2_out, not_3_out;
  wire [7:0] bank_controller_1_id_out, bank_controller_1_pattern_out, bank_module_x2_1_id_out,
       bank_module_x2_1_pattern_out, bank_module_x2_2_id_out, bank_module_x2_2_pattern_out,
       bank_module_x2_3_id_out, bank_module_x2_3_pattern_out, bank_module_x4_1_id_out,
       bank_module_x4_1_pattern_out;
  wire [13:0] bank_controller_1_a_out, bank_module_x2_1_addr_out, bank_module_x2_2_addr_out,
       bank_module_x2_3_addr_out, bank_module_x4_1_addr_out;
  wire [15:0] bank_controller_1_d_bank_out, bank_controller_1_d_mem_out, bank_module_x2_1_d_out,
       memory_1_a_bank_out, memory_1_d_bank_out, memory_1_d_out;

  and and_1 (and_1_out, not_1_out, clock_1_out);
  not not_1 (not_1_out, clock_1_out);
  and and_2 (and_2_out, WE, and_3_out);
  and and_3 (and_3_out, not_2_out, not_3_out);
  not not_2 (not_2_out, not_3_out);
  not not_3 (not_3_out, clock_1_out);
  Clock clock_1 (.out(clock_1_out));
  // Probe on memory_1_d_out
  Memory memory_1 (
    .RE_Out(memory_1_re_out), .WE_F_Out(memory_1_we_f_out), .A_Bank_Out(memory_1_a_bank_out),
    .D_Out(memory_1_d_out), .D_Bank_Out(memory_1_d_bank_out), .Sup_In(SUP), .A_In(Addr_In),
    .CLK_R(and_1_out), .D_In(Data_In), .WE_In(WE), .RE_In(RE), .WE_F_In(and_2_out),
    .D_Bank_In(bank_controller_1_d_mem_out));
  Bank_Controller bank_controller_1 (
    .D_Mem_Out(bank_controller_1_d_mem_out), .D_Bank_Out(bank_controller_1_d_bank_out),
    .A_Out(bank_controller_1_a_out), .OE_Out(bank_controller_1_oe_out), .WE_Out(bank_controller_1_we_out),
    .ID_Out(bank_controller_1_id_out), .Pattern_Out(bank_controller_1_pattern_out),
    .D_Mem_In(memory_1_d_bank_out), .A_In(memory_1_a_bank_out), .ID2_In(16'h5), .RE_In(memory_1_re_out),
    .WE_In(memory_1_we_f_out), .D_Bank_In(bank_module_x2_1_d_out));  // open: ID1_In
  Bank_Module_x2 bank_module_x2_1 (
    .ID_Out(bank_module_x2_1_id_out), .Pattern_Out(bank_module_x2_1_pattern_out),
    .OE_Out(bank_module_x2_1_oe_out), .WE_Out(bank_module_x2_1_we_out), .Addr_Out(bank_module_x2_1_addr_out),
    .D_Out(bank_module_x2_1_d_out), .Pattern_In(bank_controller_1_pattern_out),
    .ID_In(bank_controller_1_id_out), .OE_In(bank_controller_1_oe_out), .WE_In(bank_controller_1_we_out),
    .Addr_In(bank_controller_1_a_out), .D_In(bank_controller_1_d_bank_out));
  Bank_Module_x2 bank_module_x2_2 (
    .ID_Out(bank_module_x2_2_id_out), .Pattern_Out(bank_module_x2_2_pattern_out),
    .OE_Out(bank_module_x2_2_oe_out), .WE_Out(bank_module_x2_2_we_out), .Addr_Out(bank_module_x2_2_addr_out),
    .D_Out(bank_module_x2_1_d_out), .Pattern_In(bank_module_x2_1_pattern_out),
    .ID_In(bank_module_x2_1_id_out), .OE_In(bank_module_x2_1_oe_out), .WE_In(bank_module_x2_1_we_out),
    .Addr_In(bank_module_x2_1_addr_out), .D_In(bank_controller_1_d_bank_out));
  Bank_Module_x4 bank_module_x4_1 (
    .ID_Out(bank_module_x4_1_id_out), .Pattern_Out(bank_module_x4_1_pattern_out),
    .OE_Out(bank_module_x4_1_oe_out), .WE_Out(bank_module_x4_1_we_out), .Addr_Out(bank_module_x4_1_addr_out),
    .D_Out(bank_module_x2_1_d_out), .Pattern_In(bank_module_x2_2_pattern_out),
    .ID_In(bank_module_x2_2_id_out), .OE_In(bank_module_x2_2_oe_out), .WE_In(bank_module_x2_2_we_out),
    .Addr_In(bank_module_x2_2_addr_out), .D_In(bank_controller_1_d_bank_out));
  Bank_Module_x2 bank_module_x2_3 (
    .ID_Out(bank_module_x2_3_id_out), .Pattern_Out(bank_module_x2_3_pattern_out),
    .OE_Out(bank_module_x2_3_oe_out), .WE_Out(bank_module_x2_3_we_out), .Addr_Out(bank_module_x2_3_addr_out),
    .D_Out(bank_module_x2_1_d_out), .Pattern_In(bank_module_x4_1_pattern_out),
    .ID_In(bank_module_x4_1_id_out), .OE_In(bank_module_x4_1_oe_out), .WE_In(bank_module_x4_1_we_out),
    .Addr_In(bank_module_x4_1_addr_out), .D_In(bank_controller_1_d_bank_out));
endmodule

module Bank_Controller (
  input  [15:0] D_Mem_In,
  input  [15:0] D_Bank_In,
  input  [15:0] A_In,
  input  RE_In,
  input  WE_In,
  input  [15:0] ID1_In,
  input  [15:0] ID2_In,
  output [7:0] Pattern_Out,
  output [15:0] D_Bank_Out,
  output [15:0] D_Mem_Out,
  output [13:0] A_Out,
  output OE_Out,
  output WE_Out,
  output [7:0] ID_Out
);

  wire not_1_out, not_2_out;

  and and_1 (OE_Out, A_In[15], RE_In);
  and and_2 (WE_Out, A_In[15], WE_In);
  not not_1 (not_1_out, A_In[14]);
  assign ID_Out = not_1_out ? ID1_In[7:0] : 8'bz;  // Controlled_Buffer controlled_buffer_1
  not not_2 (not_2_out, not_1_out);
  assign ID_Out = not_2_out ? ID2_In[7:0] : 8'bz;  // Controlled_Buffer controlled_buffer_2

  assign A_Out = A_In[13:0];
  assign D_Bank_Out = D_Mem_In;
  assign D_Mem_Out = D_Bank_In;
  assign Pattern_Out = {8{1'b0}};
endmodule

module Bank_Module_x4 (
  input  [13:0] Addr_In,
  input  [7:0] Pattern_In,
  input  [15:0] D_In,
  input  [7:0] ID_In,
  input  OE_In,
  input  WE_In,
  output [7:0] Pattern_Out,
  output [13:0] Addr_Out,
  output [15:0] D_Out,
  output [7:0] ID_Out,
  output OE_Out,
  output WE_Out
);

  wire nand_1_out, nand_2_out, nor_1_out, not_1_out, not_2_out;
  wire [7:0] xor_1_out;
  wire [15:0] ram_1_dout;

  Hex_Digit_Display hex_digit_display_1 (.value(Pattern_In[7:4]));  // open: dp
  Hex_Digit_Display hex_digit_display_2 (.value(Pattern_In[3:0]));  // open: dp
  Adder adder_1 (.a(8'h4), .b(Pattern_In), .out(Pattern_Out));  // open: cin, cout
  assign xor_1_out = Pattern_In ^ ID_In;  // XOR_Gate xor_1, 8 bits wide
  LED led_1 (.in(nor_1_out));
  nor nor_1 (nor_1_out, xor_1_out[2], xor_1_out[3], xor_1_out[4], xor_1_out[5], xor_1_out[6], xor_1_out[7]);
  nand nand_1 (nand_1_out, nor_1_out, WE_In);
  nand nand_2 (nand_2_out, nor_1_out, OE_In);
  not not_1 (not_1_out, nand_1_out);
  not not_2 (not_2_out, nand_2_out);
  RAM #(.addrWidth(16), .dataWidth(16), .trigger("high")) ram_1 (
    .addr({ID_In[1:0], Addr_In}), .we(not_1_out), .oe(not_2_out), .din(D_In), .dout(ram_1_dout));
  assign D_Out = not_2_out ? ram_1_dout : 16'bz;  // Controlled_Buffer controlled_buffer_1

  assign Addr_Out = Addr_In;
  assign ID_Out = ID_In;
  assign OE_Out = OE_In;
  assign WE_Out = WE_In;
endmodule

module Bank_Module_x2 (
  input  [13:0] Addr_In,
  input  [7:0] Pattern_In,
  input  [15:0] D_In,
  input  [7:0] ID_In,
  input  OE_In,
  input  WE_In,
  output [7:0] Pattern_Out,
  output [13:0] Addr_Out,
  output [15:0] D_Out,
  output [7:0] ID_Out,
  output OE_Out,
  output WE_Out
);

  wire nand_1_out, nand_2_out, nor_1_out, not_1_out, not_2_out;
  wire [7:0] xor_1_out;
  wire [15:0] ram_1_dout;

  Hex_Digit_Display hex_digit_display_1 (.value(Pattern_In[7:4]));  // open: dp
  Hex_Digit_Display hex_digit_display_2 (.value(Pattern_In[3:0]));  // open: dp
  Adder adder_1 (.a(8'h2), .b(Pattern_In), .out(Pattern_Out));  // open: cin, cout
  assign xor_1_out = Pattern_In ^ ID_In;  // XOR_Gate xor_1, 8 bits wide
  nor nor_1 (nor_1_out, xor_1_out[1], xor_1_out[2], xor_1_out[3], xor_1_out[4], xor_1_out[5], xor_1_out[6], xor_1_out[7]);
  LED led_1 (.in(nor_1_out));
  nand nand_1 (nand_1_out, nor_1_out, WE_In);
  nand nand_2 (nand_2_out, nor_1_out, OE_In);
  not not_1 (not_1_out, nand_1_out);
  not not_2 (not_2_out, nand_2_out);
  RAM #(.addrWidth(15), .dataWidth(16), .trigger("high")) ram_1 (
    .addr({ID_In[0], Addr_In}), .we(not_1_out), .oe(not_2_out), .din(D_In), .dout(ram_1_dout));
  assign D_Out = not_2_out ? ram_1_dout : 16'bz;  // Controlled_Buffer controlled_buffer_1

  assign Addr_Out = Addr_In;
  assign ID_Out = ID_In;
  assign OE_Out = OE_In;
  assign WE_Out = WE_In;
endmodule

module Memory (
  input  [15:0] D_In,
  input  Sup_In,
  input  [15:0] A_In,
  input  [15:0] D_Bank_In,
  input  CLK_R,
  input  WE_In,
  input  RE_In,
  input  WE_F_In,
  output [15:0] D_Out,
  output [15:0] A_Bank_Out,
  output [15:0] D_Bank_Out,
  output RE_Out,
  output WE_F_Out
);

  wire and_1_out, and_2_out, and_3_out, decoder_1_out0, decoder_1_out1, not_1_out, not_2_out, not_3_out,
       not_4_out;
  wire [15:0] register_1_q, rom_1_data;

  Register #(.trigger("high"), .width(16)) register_1 (
    .D(D_In), .en(CLK_R), .clk(CLK_R), .Q(register_1_q));  // open: clr
  Register #(.trigger("high"), .width(16)) register_2 (.D(A_In), .en(CLK_R), .clk(CLK_R), .Q(A_Bank_Out));  // open: clr
  Decoder #(.select(2)) decoder_1 (
    .out0(decoder_1_out0), .out1(decoder_1_out1), .sel(A_Bank_Out[15:14]), .en(Sup_In));  // open: out2, out3
  not not_1 (not_1_out, decoder_1_out0);
  not not_2 (not_2_out, decoder_1_out1);
  not not_3 (not_3_out, not_1_out);
  not not_4 (not_4_out, not_2_out);
  and and_1 (and_1_out, not_3_out, RE_In);
  and and_2 (and_2_out, not_4_out, RE_In);
  and and_3 (and_3_out, not_4_out, WE_F_In);
  assign D_Bank_In = WE_In ? register_1_q : 16'bz;  // Controlled_Buffer controlled_buffer_1
  RAM #(.addrWidth(14), .dataWidth(16), .databus("bidir"), .enables("line"), .trigger("high"), .\type ("nonvolatile")) ram_1 (
    .addr(A_Bank_Out[13:0]), .we(and_3_out), .oe(and_2_out), .clk(and_3_out), .data(D_Bank_In));
  ROM #(.addrWidth(14), .dataWidth(16)) rom_1 (.addr(A_Bank_Out[13:0]), .data(rom_1_data));
  assign D_Bank_In = and_1_out ? rom_1_data : 16'bz;  // Controlled_Buffer controlled_buffer_2

  assign D_Bank_Out = D_Bank_In;
  assign D_Out = D_Bank_In;
  assign RE_Out = RE_In;
  assign WE_F_Out = WE_F_In;

  // Notes on the sheet:
  //   contents of rom_1 (hex, n*v repeats v):
  //   dead beef cafe babe 1337 42
endmodule
