// Logisim project logic_schematic.circ as structural Verilog: 6 circuits, main circuit main
module main (
  input  [15:0] in_1,
  input  [15:0] in_2,
  input  in_3,
  input  in_4,
  input  SUP,
  input  [15:0] in_6,
  input  in_7,
  input  in_8
);

  wire and_1_out, and_2_out, bank_controller_1_oe, bank_controller_1_we, bank_module_x2_1_oe_out,
       bank_module_x2_1_we_out, bank_module_x2_2_oe_out, bank_module_x2_2_we_out, bank_module_x2_3_oe_out,
       bank_module_x2_3_we_out, bank_module_x4_1_oe_out, bank_module_x4_1_we_out, clock_1_out, memory_1_rw,
       memory_1_we_bank_out, not_1_out, not_2_out, not_3_out;
  wire [7:0] bank_controller_1_id_out, bank_controller_1_pattern_out, bank_module_x2_1_id_out,
       bank_module_x2_1_pattern_out, bank_module_x2_2_id_out, bank_module_x2_2_pattern_out,
       bank_module_x2_3_id_out, bank_module_x2_3_pattern_out, bank_module_x4_1_id_out,
       bank_module_x4_1_pattern_out;
  wire [13:0] bank_controller_1_a_out, bank_module_x2_1_addr_out, bank_module_x2_2_addr_out,
       bank_module_x2_3_addr_out, bank_module_x4_1_addr_out;
  wire [15:0] bank_controller_1_d_bank_out, bank_controller_1_d_mem_out, bank_module_x2_1_d_out,
       bid_register_1_bid1_out, bid_register_1_bid2_out, memory_1_a_bank_out, memory_1_bid1_out,
       memory_1_bid2_out, memory_1_d_bank_out, memory_1_d_out;

  // Probe on memory_1_d_out
  and and_1 (and_1_out, not_2_out, not_3_out);
  and and_2 (and_2_out, not_1_out, clock_1_out);
  not not_1 (not_1_out, clock_1_out);
  not not_2 (not_2_out, not_3_out);
  not not_3 (not_3_out, clock_1_out);
  Clock clock_1 (.out(clock_1_out));
  BID_Register bid_register_1 (
    .BID1_Out(bid_register_1_bid1_out), .BID2_Out(bid_register_1_bid2_out), .WE_F(in_8), .Sup_In(SUP),
    .S_BID(in_7), .BID_In(in_6), .WE_R(and_2_out));
  Memory memory_1 (
    .D_Out(memory_1_d_out), .RW(memory_1_rw), .BID1_Out(memory_1_bid1_out), .BID2_Out(memory_1_bid2_out),
    .D_Bank_Out(memory_1_d_bank_out), .A_Bank_Out(memory_1_a_bank_out), .WE_Bank_Out(memory_1_we_bank_out),
    .A_In(in_1), .CLK_R(and_2_out), .Sup_In(SUP), .RE(in_4), .WE(in_3), .CLK_F(and_1_out), .D_In(in_2),
    .BID1_In(bid_register_1_bid1_out), .BID2_In(bid_register_1_bid2_out),
    .D_Bank_In(bank_controller_1_d_mem_out));
  Bank_Controller bank_controller_1 (
    .D_Mem_Out(bank_controller_1_d_mem_out), .D_Bank_Out(bank_controller_1_d_bank_out),
    .A_Out(bank_controller_1_a_out), .OE(bank_controller_1_oe), .ID_Out(bank_controller_1_id_out),
    .Pattern_Out(bank_controller_1_pattern_out), .WE(bank_controller_1_we), .ID1_In(memory_1_bid1_out),
    .ID2_In(memory_1_bid2_out), .D_Mem_In(memory_1_d_bank_out), .A_In(memory_1_a_bank_out), .RW(memory_1_rw),
    .D_Bank_In(bank_module_x2_1_d_out), .Enable(memory_1_we_bank_out));
  Bank_Module_x2 bank_module_x2_1 (
    .ID_Out(bank_module_x2_1_id_out), .Pattern_Out(bank_module_x2_1_pattern_out),
    .OE_Out(bank_module_x2_1_oe_out), .WE_Out(bank_module_x2_1_we_out), .Addr_Out(bank_module_x2_1_addr_out),
    .D_Out(bank_module_x2_1_d_out), .Pattern_In(bank_controller_1_pattern_out),
    .ID_In(bank_controller_1_id_out), .OE_In(bank_controller_1_oe), .WE_In(bank_controller_1_we),
    .Addr_In(bank_controller_1_a_out), .D_In(bank_controller_1_d_bank_out));
  Bank_Module_x2 bank_module_x2_2 (
    .ID_Out(bank_module_x2_2_id_out), .Pattern_Out(bank_module_x2_2_pattern_out),
    .OE_Out(bank_module_x2_2_oe_out), .WE_Out(bank_module_x2_2_we_out), .Addr_Out(bank_module_x2_2_addr_out),
    .D_Out(bank_module_x2_1_d_out), .Pattern_In(bank_module_x2_1_pattern_out),
    .ID_In(bank_module_x2_1_id_out), .OE_In(bank_module_x2_1_oe_out), .WE_In(bank_module_x2_1_we_out),
    .Addr_In(bank_module_x2_1_addr_out), .D_In(bank_controller_1_d_bank_out));
  Bank_Module_x4 bank_module_x4_1 (
    .ID_Out(bank_module_x4_1_id_out), .Pattern_Out(bank_module_x4_1_pattern_out),
    .OE_Out(bank_module_x4_1_oe_out), .WE_Out(bank_module_x4_1_we_out), .Addr_Out(bank_module_x4_1_addr_out),
    .D_Out(bank_module_x2_1_d_out), .Pattern_In(bank_module_x2_2_pattern_out),
    .ID_In(bank_module_x2_2_id_out), .OE_In(bank_module_x2_2_oe_out), .WE_In(bank_module_x2_2_we_out),
    .Addr_In(bank_module_x2_2_addr_out), .D_In(bank_controller_1_d_bank_out));
  Bank_Module_x2 bank_module_x2_3 (
    .ID_Out(bank_module_x2_3_id_out), .Pattern_Out(bank_module_x2_3_pattern_out),
    .OE_Out(bank_module_x2_3_oe_out), .WE_Out(bank_module_x2_3_we_out), .Addr_Out(bank_module_x2_3_addr_out),
    .D_Out(bank_module_x2_1_d_out), .Pattern_In(bank_module_x4_1_pattern_out),
    .ID_In(bank_module_x4_1_id_out), .OE_In(bank_module_x4_1_oe_out), .WE_In(bank_module_x4_1_we_out),
    .Addr_In(bank_module_x4_1_addr_out), .D_In(bank_controller_1_d_bank_out));
endmodule

module Bank_Controller (
  input  [15:0] D_Mem_In,
  input  [15:0] D_Bank_In,
  input  [15:0] A_In,
  input  RW,
  input  Enable,
  input  [15:0] ID1_In,
  input  [15:0] ID2_In,
  output [7:0] Pattern_Out,
  output [15:0] D_Bank_Out,
  output [15:0] D_Mem_Out,
  output [13:0] A_Out,
  output OE,
  output WE,
  output [7:0] ID_Out
);

  wire and_2_out, not_1_out, not_2_out, not_3_out;

  not not_1 (not_1_out, RW);
  and and_1 (OE, A_In[15], not_1_out);
  and and_2 (and_2_out, A_In[15], RW);
  not not_2 (not_2_out, A_In[14]);
  assign ID_Out = not_2_out ? ID1_In[7:0] : 8'bz;  // Controlled_Buffer controlled_buffer_1
  not not_3 (not_3_out, not_2_out);
  assign ID_Out = not_3_out ? ID2_In[7:0] : 8'bz;  // Controlled_Buffer controlled_buffer_2
  and and_3 (WE, and_2_out, Enable);

  assign A_Out = A_In[13:0];
  assign D_Bank_Out = D_Mem_In;
  assign D_Mem_Out = D_Bank_In;
  assign Pattern_Out = {8{1'b0}};
endmodule

module Bank_Module_x4 (
  input  [13:0] Addr_In,
  input  [7:0] Pattern_In,
  input  [15:0] D_In,
  input  [7:0] ID_In,
  input  OE_In,
  input  WE_In,
  output [7:0] Pattern_Out,
  output [13:0] Addr_Out,
  output [15:0] D_Out,
  output [7:0] ID_Out,
  output OE_Out,
  output WE_Out
);

  wire nand_1_out, nand_2_out, nor_1_out, not_1_out, not_2_out;
  wire [7:0] xor_1_out;
  wire [15:0] ram_1_dout;

  Hex_Digit_Display hex_digit_display_1 (.value(Pattern_In[7:4]));  // open: dp
  Hex_Digit_Display hex_digit_display_2 (.value(Pattern_In[3:0]));  // open: dp
  Adder adder_1 (.a(8'h4), .b(Pattern_In), .out(Pattern_Out));  // open: cin, cout
  assign xor_1_out = Pattern_In ^ ID_In;  // XOR_Gate xor_1, 8 bits wide
  LED led_1 (.in(nor_1_out));
  nor nor_1 (nor_1_out, xor_1_out[2], xor_1_out[3], xor_1_out[4], xor_1_out[5], xor_1_out[6], xor_1_out[7]);
  nand nand_1 (nand_1_out, nor_1_out, WE_In);
  nand nand_2 (nand_2_out, nor_1_out, OE_In);
  not not_1 (not_1_out, nand_1_out);
  not not_2 (not_2_out, nand_2_out);
  RAM #(.addrWidth(16), .dataWidth(16), .trigger("high")) ram_1 (
    .addr({Pattern_In[1:0], Addr_In}), .we(not_1_out), .oe(not_2_out), .din(D_In), .dout(ram_1_dout));
  assign D_Out = not_2_out ? ram_1_dout : 16'bz;  // Controlled_Buffer controlled_buffer_1

  assign Addr_Out = Addr_In;
  assign ID_Out = ID_In;
  assign OE_Out = OE_In;
  assign WE_Out = WE_In;
endmodule

module Bank_Module_x2 (
  input  [13:0] Addr_In,
  input  [7:0] Pattern_In,
  input  [15:0] D_In,
  input  [7:0] ID_In,
  input  OE_In,
  input  WE_In,
  output [7:0] Pattern_Out,
  output [13:0] Addr_Out,
  output [15:0] D_Out,
  output [7:0] ID_Out,
  output OE_Out,
  output WE_Out
);

  wire nand_1_out, nand_2_out, nor_1_out, not_1_out, not_2_out;
  wire [7:0] xor_1_out;
  wire [15:0] ram_1_dout;

  Hex_Digit_Display hex_digit_display_1 (.value(Pattern_In[7:4]));  // open: dp
  Hex_Digit_Display hex_digit_display_2 (.value(Pattern_In[3:0]));  // open: dp
  Adder adder_1 (.a(8'h2), .b(Pattern_In), .out(Pattern_Out));  // open: cin, cout
  assign xor_1_out = Pattern_In ^ ID_In;  // XOR_Gate xor_1, 8 bits wide
  nor nor_1 (nor_1_out, xor_1_out[1], xor_1_out[2], xor_1_out[3], xor_1_out[4], xor_1_out[5], xor_1_out[6], xor_1_out[7]);
  LED led_1 (.in(nor_1_out));
  nand nand_1 (nand_1_out, nor_1_out, WE_In);
  nand nand_2 (nand_2_out, nor_1_out, OE_In);
  not not_1 (not_1_out, nand_1_out);
  not not_2 (not_2_out, nand_2_out);
  RAM #(.addrWidth(15), .dataWidth(16), .trigger("high")) ram_1 (
    .addr({Pattern_In[0], Addr_In}), .we(not_1_out), .oe(not_2_out), .din(D_In), .dout(ram_1_dout));
  assign D_Out = not_2_out ? ram_1_dout : 16'bz;  // Controlled_Buffer controlled_buffer_1

  assign Addr_Out = Addr_In;
  assign ID_Out = ID_In;
  assign OE_Out = OE_In;
  assign WE_Out = WE_In;
endmodule

module BID_Register (
  input  WE_F,
  input  Sup_In,
  input  S_BID,
  input  [15:0] BID_In,
  input  WE_R,
  output [15:0] BID1_Out,
  output [15:0] BID2_Out
);

  wire and_1_out, and_2_out, and_3_out, not_1_out;
  wire [15:0] register_1_q;

  and and_1 (and_1_out, WE_F, Sup_In);
  not not_1 (not_1_out, S_BID);
  Register #(.trigger("high"), .width(16)) register_1 (
    .D(BID_In), .en(WE_R), .clk(WE_R), .Q(register_1_q));  // open: clr
  Register #(.trigger("high"), .width(16)) register_2 (
    .D(register_1_q), .en(and_2_out), .clk(and_2_out), .Q(BID1_Out));  // open: clr
  and and_2 (and_2_out, and_1_out, not_1_out);
  Register #(.trigger("high"), .width(16)) register_3 (
    .D(register_1_q), .en(and_3_out), .clk(and_3_out), .Q(BID2_Out));  // open: clr
  and and_3 (and_3_out, and_1_out, S_BID);
endmodule

module Memory (
  input  [15:0] D_Bank_In,
  input  [15:0] D_In,
  input  [15:0] A_In,
  input  CLK_R,
  input  Sup_In,
  input  RE,
  input  WE,
  input  CLK_F,
  input  [15:0] BID1_In,
  input  [15:0] BID2_In,
  output [15:0] D_Bank_Out,
  output [15:0] A_Bank_Out,
  output [15:0] D_Out,
  output RW,
  output WE_Bank_Out,
  output [15:0] BID1_Out,
  output [15:0] BID2_Out
);

  wire and_1_out, and_3_out, decoder_1_out0, decoder_1_out1, nand_1_out, nand_2_out, nand_3_out, nand_4_out,
       not_1_out, not_2_out, not_3_out, not_4_out, not_5_out, not_6_out, not_7_out, not_8_out, not_9_out,
       not_10_out;
  wire [15:0] ram_1_data, register_1_q, rom_1_data;

  Register #(.trigger("high"), .width(16)) register_1 (
    .D(D_In), .en(CLK_R), .clk(CLK_R), .Q(register_1_q));  // open: clr
  Register #(.trigger("high"), .width(16)) register_2 (.D(A_In), .en(CLK_R), .clk(CLK_R), .Q(A_Bank_Out));  // open: clr
  assign D_Bank_Out = and_1_out ? register_1_q : 16'bz;  // Controlled_Buffer controlled_buffer_1
  Decoder #(.select(2)) decoder_1 (
    .out0(decoder_1_out0), .out1(decoder_1_out1), .sel(A_Bank_Out[15:14]), .en(Sup_In));  // open: out2, out3
  not not_1 (not_1_out, decoder_1_out0);
  not not_2 (not_2_out, decoder_1_out1);
  and and_1 (and_1_out, WE, A_Bank_Out[15]);
  and and_2 (WE_Bank_Out, and_1_out, CLK_F);
  not not_3 (not_3_out, not_2_out);
  not not_4 (not_4_out, not_1_out);
  nand nand_1 (nand_1_out, A_Bank_Out[15], RE);
  nand nand_2 (nand_2_out, not_3_out, WE);
  nand nand_3 (nand_3_out, not_3_out, RE);
  nand nand_4 (nand_4_out, not_4_out, RE);
  not not_5 (not_5_out, nand_2_out);
  not not_6 (not_6_out, nand_3_out);
  and and_3 (and_3_out, not_5_out, CLK_F);
  RAM #(.addrWidth(14), .dataWidth(16), .databus("bidir"), .trigger("high"), .\type ("nonvolatile")) ram_1 (
    .addr(A_Bank_Out[13:0]), .we(and_3_out), .oe(not_6_out), .data(ram_1_data));
  ROM #(.addrWidth(14), .dataWidth(16)) rom_1 (.addr(A_Bank_Out[13:0]), .data(rom_1_data));
  assign D_Out = not_7_out ? D_Bank_In : 16'bz;  // Controlled_Buffer controlled_buffer_2
  not not_7 (not_7_out, nand_1_out);
  not not_8 (not_8_out, nand_2_out);
  assign ram_1_data = not_8_out ? register_1_q : 16'bz;  // Controlled_Buffer controlled_buffer_3
  not not_9 (not_9_out, nand_3_out);
  assign D_Out = not_9_out ? ram_1_data : 16'bz;  // Controlled_Buffer controlled_buffer_4
  not not_10 (not_10_out, nand_4_out);
  assign D_Out = not_10_out ? rom_1_data : 16'bz;  // Controlled_Buffer controlled_buffer_5

  assign BID1_Out = BID1_In;
  assign BID2_Out = BID2_In;
  assign RW = WE;

  // Notes on the sheet:
  //   contents of rom_1 (hex, n*v repeats v):
  //   dead beef cafe babe 1337 42
endmodule
