// Logisim project Timer.circ as structural Verilog: 3 circuits, main circuit main_Timer
module main_Timer (
);

  wire and_1_out, and_2_out, clock_1_out, clock_2_out, counter_1_carry, counter_2_carry, j_k_ff_1_q,
       not_1_out, not_2_out, not_3_out;

  Counter #(.max('h3e8), .width(12)) counter_1 (
    .clk(clock_1_out), .carry(counter_1_carry));  // open: clr, load, up, count, D, Q
  Clock clock_1 (.out(clock_1_out));
  Counter #(.max('h32), .width(32)) counter_2 (
    .clk(clock_2_out), .carry(counter_2_carry));  // open: clr, load, up, count, D, Q
  Clock clock_2 (.out(clock_2_out));
  J_K_Flip_Flop j_k_ff_1 (
    .J(counter_2_carry), .K(counter_2_carry), .clk(counter_2_carry), .Q(j_k_ff_1_q));  // open: Qn, preset, reset
  not not_1 (not_1_out, j_k_ff_1_q);
  not not_2 (not_2_out, j_k_ff_1_q);
  and and_1 (and_1_out, not_1_out, j_k_ff_1_q);
  not not_3 (not_3_out, not_2_out);
  and and_2 (and_2_out, not_3_out, not_2_out);
  Freq_Counter freq_counter_1 (.Ref_CLK(counter_1_carry), .CLK_R(and_1_out), .CLK_F(and_2_out));  // open: Freq_Out, HL
endmodule

module Freq_Counter (
  input  Ref_CLK,
  input  HL,
  input  CLK_R,
  input  CLK_F,
  output [15:0] Freq_Out
);

  wire and_1_out, and_2_out, counter_1_carry, not_1_out, not_2_out, not_3_out, not_4_out, not_5_out,
       not_6_out;
  wire [23:0] counter_1_q;
  wire [31:0] register_1_q;

  and and_1 (and_1_out, not_1_out, Ref_CLK);
  and and_2 (and_2_out, not_2_out, not_3_out);
  not not_1 (not_1_out, Ref_CLK);
  not not_2 (not_2_out, not_3_out);
  not not_3 (not_3_out, Ref_CLK);
  Counter #(.max('hffffff), .width(24)) counter_1 (
    .clr(and_2_out), .load(Ref_CLK), .count(1'b1), .clk(CLK_R), .D({24{1'b0}}), .carry(counter_1_carry),
    .Q(counter_1_q));  // open: up
  Register #(.trigger("high"), .width(32)) register_1 (
    .D({{8{1'b0}}, counter_1_q}), .en(and_1_out), .clk(and_1_out), .Q(register_1_q));  // open: clr
  assign Freq_Out = not_4_out ? register_1_q[15:0] : 16'bz;  // Controlled_Buffer controlled_buffer_1
  not not_4 (not_4_out, HL);
  not not_5 (not_5_out, HL);
  assign Freq_Out = not_6_out ? register_1_q[31:16] : 16'bz;  // Controlled_Buffer controlled_buffer_2
  not not_6 (not_6_out, not_5_out);
endmodule

module Timer (
  input  Low_High,
  input  [15:0] D_In,
  input  T1T2,
  input  Sup_In,
  input  WE,
  input  CLK_F,
  input  StopMode,
  input  CLK_Ref,
  input  CLK_R,
  output [15:0] D_Out,
  output T1_Int_Out,
  output T2_Int_Out
);

  wire and_1_out, and_2_out, and_3_out, and_4_out, and_5_out, and_6_out, and_7_out, and_8_out, and_9_out,
       and_10_out, and_11_out, and_12_out, and_14_out, and_15_out, and_16_out, and_17_out, and_18_out,
       decoder_1_out0, decoder_1_out1, decoder_1_out2, decoder_1_out3, decoder_2_out1, decoder_2_out2,
       decoder_2_out3, decoder_3_out1, decoder_3_out2, decoder_3_out3, j_k_ff_1_q, j_k_ff_2_q, nor_1_out,
       nor_2_out, nor_3_out, nor_4_out, nor_5_out, nor_6_out, nor_7_out, nor_8_out, not_1_out, not_2_out,
       not_3_out, not_4_out, not_5_out, not_6_out, not_7_out, not_8_out, not_9_out, not_10_out, not_11_out,
       not_12_out, not_13_out, not_14_out, or_1_out, or_2_out, or_3_out, or_4_out, or_5_out, or_6_out;
  wire [1:0] Mode_T1_q, register_3_q;
  wire [15:0] register_1_q, register_2_q, Stop_T1_H_q, Stop_T1_L_q;
  wire [31:0] counter_1_q, counter_2_q, xor_1_out, xor_2_out;

  and and_1 (and_1_out, Sup_In, WE);
  and and_2 (and_2_out, not_1_out, and_4_out);
  not not_1 (not_1_out, StopMode);
  and and_3 (and_3_out, StopMode, and_4_out);
  and and_4 (and_4_out, and_1_out, CLK_F);
  Freq_Counter freq_counter_1 (.Freq_Out(D_Out), .HL(Low_High), .Ref_CLK(CLK_Ref), .CLK_R(CLK_R), .CLK_F(CLK_F));
  Decoder #(.select(2)) decoder_1 (
    .out0(decoder_1_out0), .out1(decoder_1_out1), .out2(decoder_1_out2), .out3(decoder_1_out3),
    .sel({T1T2, Low_High}), .en(and_2_out));
  not not_2 (not_2_out, T1T2);
  not not_3 (not_3_out, decoder_1_out0);
  not not_4 (not_4_out, decoder_1_out1);
  not not_5 (not_5_out, decoder_1_out2);
  not not_6 (not_6_out, decoder_1_out3);
  not not_7 (not_7_out, Sup_In);
  not not_8 (not_8_out, not_2_out);
  Register #(.width(16)) Stop_T1_L (.D(D_In), .en(not_9_out), .clk(not_9_out), .Q(Stop_T1_L_q));  // open: clr
  not not_9 (not_9_out, not_3_out);
  Register #(.width(16)) Stop_T1_H (.D(D_In), .en(not_10_out), .clk(not_10_out), .Q(Stop_T1_H_q));  // open: clr
  not not_10 (not_10_out, not_4_out);
  and and_5 (and_5_out, not_7_out, Sup_In);
  and and_6 (and_6_out, and_3_out, not_2_out);
  and and_7 (and_7_out, and_3_out, not_8_out);
  Register #(.trigger("high"), .width(2)) Mode_T1 (
    .D(D_In[1:0]), .en(or_1_out), .clk(or_1_out), .Q(Mode_T1_q));  // open: clr
  or or_1 (or_1_out, and_5_out, and_6_out);
  Decoder #(.select(2)) decoder_2 (
    .out1(decoder_2_out1), .out2(decoder_2_out2), .out3(decoder_2_out3), .sel(Mode_T1_q));  // open: out0, en
  not not_11 (not_11_out, decoder_2_out3);
  and and_8 (and_8_out, not_11_out, decoder_2_out3);
  or or_2 (or_2_out, T1_Int_Out, decoder_2_out1);
  and and_9 (and_9_out, or_2_out, CLK_F);
  or or_3 (or_3_out, decoder_2_out2, j_k_ff_1_q);
  and and_10 (and_10_out, or_3_out, CLK_R);
  J_K_Flip_Flop j_k_ff_1 (.Q(j_k_ff_1_q), .preset(and_8_out), .reset(T1_Int_Out));  // open: J, K, clk, Qn
  Counter #(.max('hffffffff), .width(32)) counter_1 (
    .clr(and_9_out), .up(1'b1), .clk(and_10_out), .Q(counter_1_q));  // open: load, count, D, carry
  assign xor_1_out = {Stop_T1_H_q, Stop_T1_L_q} ^ counter_1_q;  // XOR_Gate xor_1, 32 bits wide
  nor nor_1 (nor_1_out, xor_1_out[0], xor_1_out[1], xor_1_out[2], xor_1_out[3], xor_1_out[4], xor_1_out[5], xor_1_out[6], xor_1_out[7]);
  nor nor_2 (nor_2_out, xor_1_out[8], xor_1_out[9], xor_1_out[10], xor_1_out[11], xor_1_out[12], xor_1_out[13], xor_1_out[14], xor_1_out[15]);
  nor nor_3 (nor_3_out, xor_1_out[16], xor_1_out[17], xor_1_out[18], xor_1_out[19], xor_1_out[20], xor_1_out[21], xor_1_out[22], xor_1_out[23]);
  nor nor_4 (nor_4_out, xor_1_out[24], xor_1_out[25], xor_1_out[26], xor_1_out[27], xor_1_out[28], xor_1_out[29], xor_1_out[30], xor_1_out[31]);
  and and_11 (and_11_out, nor_1_out, nor_2_out);
  and and_12 (and_12_out, nor_3_out, nor_4_out);
  Register #(.width(16)) register_1 (.D(D_In), .en(not_12_out), .clk(not_12_out), .Q(register_1_q));  // open: clr
  not not_12 (not_12_out, not_5_out);
  Register #(.width(16)) register_2 (.D(D_In), .en(not_13_out), .clk(not_13_out), .Q(register_2_q));  // open: clr
  not not_13 (not_13_out, not_6_out);
  and and_13 (T1_Int_Out, and_11_out, and_12_out);
  Register #(.trigger("high"), .width(2)) register_3 (
    .D(D_In[1:0]), .en(or_4_out), .clk(or_4_out), .Q(register_3_q));  // open: clr
  or or_4 (or_4_out, and_5_out, and_7_out);
  Decoder #(.select(2)) decoder_3 (
    .out1(decoder_3_out1), .out2(decoder_3_out2), .out3(decoder_3_out3), .sel(register_3_q));  // open: out0, en
  not not_14 (not_14_out, decoder_3_out3);
  or or_5 (or_5_out, T2_Int_Out, decoder_3_out1);
  or or_6 (or_6_out, decoder_3_out2, j_k_ff_2_q);
  and and_14 (and_14_out, or_6_out, CLK_R);
  and and_15 (and_15_out, not_14_out, decoder_3_out3);
  J_K_Flip_Flop j_k_ff_2 (.Q(j_k_ff_2_q), .preset(and_15_out), .reset(T2_Int_Out));  // open: J, K, clk, Qn
  Counter #(.max('hffffffff), .width(32)) counter_2 (
    .clr(and_16_out), .up(1'b1), .clk(and_14_out), .Q(counter_2_q));  // open: load, count, D, carry
  and and_16 (and_16_out, or_5_out, CLK_F);
  assign xor_2_out = {register_2_q, register_1_q} ^ counter_2_q;  // XOR_Gate xor_2, 32 bits wide
  nor nor_5 (nor_5_out, xor_2_out[0], xor_2_out[1], xor_2_out[2], xor_2_out[3], xor_2_out[4], xor_2_out[5], xor_2_out[6], xor_2_out[7]);
  nor nor_6 (nor_6_out, xor_2_out[24], xor_2_out[25], xor_2_out[26], xor_2_out[27], xor_2_out[28], xor_2_out[29], xor_2_out[30], xor_2_out[31]);
  and and_17 (and_17_out, nor_5_out, nor_7_out);
  nor nor_7 (nor_7_out, xor_2_out[8], xor_2_out[9], xor_2_out[10], xor_2_out[11], xor_2_out[12], xor_2_out[13], xor_2_out[14], xor_2_out[15]);
  nor nor_8 (nor_8_out, xor_2_out[16], xor_2_out[17], xor_2_out[18], xor_2_out[19], xor_2_out[20], xor_2_out[21], xor_2_out[22], xor_2_out[23]);
  and and_18 (and_18_out, nor_8_out, nor_6_out);
  and and_19 (T2_Int_Out, and_17_out, and_18_out);
endmodule
