// Logisim project logic_schematic_computer_simple.circ as structural Verilog: 14 circuits, main circuit main
module main (
);

  wire activationmodule_1_we, activationmodule_2_re, activationmodule_2_we, activationmodule_2_we_f,
       activationmodule_3_re, activationmodule_3_we_f, activationmodule_4_we_f, activationmodule_4_we_r,
       activationmodule_5_we_f, activationmodule_5_we_r, and_1_out, and_2_out, and_3_out, and_4_out,
       and_5_out, and_6_out, and_8_out, buffer_1_out, buffer_2_out, buffer_3_out, buffer_4_out, buffer_5_out,
       buffer_6_out, buffer_7_out, buffer_8_out, clock_1_out, instruction_decoder_1_const_reg,
       instruction_decoder_1_r_sup, instruction_decoder_1_reg_inc, instruction_decoder_1_zero_one,
       interrupt_controller_1_s_sup, j_k_ff_1_q, j_k_ff_1_qn, not_1_out, not_2_out, not_3_out, not_4_out,
       not_5_out, not_6_out, not_7_out, register_file_1_sup_out;
  wire [1:0] instruction_decoder_1_out_14;
  wire [2:0] activationmodule_4_mode_w, activationmodule_5_mode_w, instruction_decoder_1_reg_sel_a,
       instruction_decoder_1_reg_sel_b, instruction_decoder_1_reg_sel_in;
  wire [4:0] not_8_out, register_file_1_flag_out_2;
  wire [6:0] activationmodule_1_bus2_out, instruction_decoder_1_re1_out, instruction_decoder_1_re2_out,
       instruction_decoder_1_we1_out, instruction_decoder_1_we2_out, register_1_q;
  wire [10:0] register_file_1_flag_out;
  wire [15:0] activationmodule_1_bus1_out, activationmodule_1_from_bus, activationmodule_4_from_bus,
       adder_1_out, alu_1_a_out, alu_1_b_out, and_7_out, controlled_buffer_1_out,
       instruction_decoder_1_const_out, interrupt_controller_1_ip_out, memory_1_d_out, register_2_q,
       register_file_1_a_out, register_file_1_b_out, register_file_1_ip_out, subtractor_1_out, xor_1_out;
  wire [15:7] activationmodule_1_bus2_out_2;
  wire [31:0] dual_register_1_d_l_out;

  Clock clock_1 (.out(clock_1_out));
  J_K_Flip_Flop j_k_ff_1 (
    .J(1'b1), .K(1'b1), .clk(clock_1_out), .Q(j_k_ff_1_q), .Qn(j_k_ff_1_qn));  // open: preset, reset
  buf buffer_1 (buffer_1_out, clock_1_out);
  buf buffer_2 (buffer_2_out, buffer_1_out);
  buf buffer_3 (buffer_3_out, buffer_2_out);
  buf buffer_4 (buffer_4_out, buffer_3_out);
  buf buffer_5 (buffer_5_out, buffer_4_out);
  buf buffer_6 (buffer_6_out, buffer_5_out);
  buf buffer_7 (buffer_7_out, buffer_6_out);
  buf buffer_8 (buffer_8_out, buffer_7_out);
  not not_1 (not_1_out, and_2_out);
  not not_2 (not_2_out, not_1_out);
  and and_1 (and_1_out, not_1_out, not_2_out);
  and and_2 (and_2_out, j_k_ff_1_qn, buffer_8_out);
  and and_3 (and_3_out, j_k_ff_1_q, buffer_8_out);
  not not_3 (not_3_out, and_3_out);
  not not_4 (not_4_out, and_2_out);
  not not_5 (not_5_out, not_3_out);
  and and_4 (and_4_out, and_2_out, not_4_out);
  and and_5 (and_5_out, not_3_out, not_5_out);
  // Probe on instruction_decoder_1_we2_out
  not not_6 (not_6_out, and_3_out);
  and and_6 (and_6_out, and_3_out, not_6_out);
  // Probe on instruction_decoder_1_we1_out
  // Probe on instruction_decoder_1_re1_out
  // Probe on instruction_decoder_1_re2_out
  // Probe on {activationmodule_1_bus2_out_2, activationmodule_1_bus2_out}
  // Probe on activationmodule_1_bus1_out
  // Probe on and_3_out
  // Probe on and_2_out
  ActivationModule activationmodule_1 (
    .WE(activationmodule_1_we), .from_Bus(activationmodule_1_from_bus),
    .BUS1_Out(activationmodule_1_bus1_out),
    .BUS2_Out({activationmodule_1_bus2_out_2, activationmodule_1_bus2_out}),
    .RE1(instruction_decoder_1_re1_out), .RE2(instruction_decoder_1_re2_out),
    .WE1(instruction_decoder_1_we1_out), .WE2(instruction_decoder_1_we2_out), .PatternW(4'b0001),
    .Diasble_R(1'b1), .CLK_F(and_5_out), .CLK_R(and_6_out), .BUS1_In(activationmodule_1_bus1_out),
    .BUS2_In({activationmodule_1_bus2_out_2, activationmodule_1_bus2_out}));  // open: Mode_W, Mode_R, RE, WE_F, WE_R, PatternR, Disable_W, To_Bus
  ActivationModule activationmodule_2 (
    .RE(activationmodule_2_re), .WE(activationmodule_2_we), .WE_F(activationmodule_2_we_f),
    .BUS1_Out(activationmodule_1_bus1_out),
    .BUS2_Out({activationmodule_1_bus2_out_2, activationmodule_1_bus2_out}),
    .RE1(instruction_decoder_1_re1_out), .RE2(instruction_decoder_1_re2_out),
    .WE1(instruction_decoder_1_we1_out), .WE2(instruction_decoder_1_we2_out), .PatternR(4'b0010),
    .PatternW(4'b0010), .CLK_F(and_5_out), .CLK_R(and_6_out), .To_Bus(memory_1_d_out),
    .BUS1_In(activationmodule_1_bus1_out),
    .BUS2_In({activationmodule_1_bus2_out_2, activationmodule_1_bus2_out}));  // open: Mode_W, Mode_R, WE_R, from_Bus, Diasble_R, Disable_W
  ActivationModule activationmodule_3 (
    .RE(activationmodule_3_re), .WE_F(activationmodule_3_we_f), .BUS1_Out(activationmodule_1_bus1_out),
    .BUS2_Out({activationmodule_1_bus2_out_2, activationmodule_1_bus2_out}),
    .RE1(instruction_decoder_1_re1_out), .RE2(instruction_decoder_1_re2_out),
    .WE1(instruction_decoder_1_we1_out), .WE2(instruction_decoder_1_we2_out), .PatternR(4'b0100),
    .PatternW(4'b0100), .CLK_F(and_5_out), .CLK_R(and_6_out), .To_Bus(interrupt_controller_1_ip_out),
    .BUS1_In(activationmodule_1_bus1_out),
    .BUS2_In({activationmodule_1_bus2_out_2, activationmodule_1_bus2_out}));  // open: Mode_W, Mode_R, WE, WE_R, from_Bus, Diasble_R, Disable_W
  ActivationModule activationmodule_4 (
    .Mode_W(activationmodule_4_mode_w), .WE_F(activationmodule_4_we_f), .WE_R(activationmodule_4_we_r),
    .from_Bus(activationmodule_4_from_bus), .BUS1_Out(activationmodule_1_bus1_out),
    .BUS2_Out({activationmodule_1_bus2_out_2, activationmodule_1_bus2_out}),
    .RE1(instruction_decoder_1_re1_out), .RE2(instruction_decoder_1_re2_out),
    .WE1(instruction_decoder_1_we1_out), .WE2(instruction_decoder_1_we2_out), .PatternR(4'b0101),
    .PatternW(4'b0101), .CLK_F(and_5_out), .CLK_R(and_6_out), .BUS1_In(activationmodule_1_bus1_out),
    .BUS2_In({activationmodule_1_bus2_out_2, activationmodule_1_bus2_out}));  // open: Mode_R, RE, WE, Diasble_R, Disable_W, To_Bus
  ActivationModule activationmodule_5 (
    .Mode_W(activationmodule_5_mode_w), .WE_F(activationmodule_5_we_f), .WE_R(activationmodule_5_we_r),
    .RE1(instruction_decoder_1_re1_out), .RE2(instruction_decoder_1_re2_out),
    .WE1(instruction_decoder_1_we1_out), .WE2(instruction_decoder_1_we2_out), .PatternR(4'b0110),
    .PatternW(4'b0110), .CLK_F(and_5_out), .CLK_R(and_6_out));  // open: Mode_R, RE, WE, from_Bus, BUS1_Out, BUS2_Out, Diasble_R, Disable_W, To_Bus, BUS1_In, BUS2_In
  ALU alu_1 (
    .A_Out(alu_1_a_out), .B_Out(alu_1_b_out), .Q1_Out(activationmodule_1_bus1_out),
    .Q2_Out({activationmodule_1_bus2_out_2, activationmodule_1_bus2_out}),
    .Q1_Sel(instruction_decoder_1_re1_out), .Q2_Sel(instruction_decoder_1_re2_out), .Pattern_R(4'b0001),
    .A_In(register_file_1_a_out), .B_In(register_file_1_b_out), .op2(adder_1_out), .op3(subtractor_1_out),
    .op4(xor_1_out), .op5(and_7_out), .op6(controlled_buffer_1_out),
    .op7({register_file_1_flag_out, not_8_out}));
  Register_File register_file_1 (
    .FLAG_Out({register_file_1_flag_out, register_file_1_flag_out_2}), .B_Out(register_file_1_b_out),
    .Sup_Out(register_file_1_sup_out), .A_Out(register_file_1_a_out), .IP_Out(register_file_1_ip_out),
    .CLK_R(and_6_out), .CLK_F(and_5_out), .WE(activationmodule_1_we), .Inc(instruction_decoder_1_reg_inc),
    .R_Sup(instruction_decoder_1_r_sup), .S_Sup(interrupt_controller_1_s_sup),
    .Const_In(instruction_decoder_1_const_out), .Const_Reg(instruction_decoder_1_const_reg),
    .D_In(activationmodule_1_from_bus), .D_Sel(instruction_decoder_1_reg_sel_in),
    .A_Sel(instruction_decoder_1_reg_sel_a), .B_Sel(instruction_decoder_1_reg_sel_b),
    .Zero_One(instruction_decoder_1_zero_one));
  Interrupt_Controller interrupt_controller_1 (
    .IP_Out(interrupt_controller_1_ip_out), .S_Sup(interrupt_controller_1_s_sup), .RE(activationmodule_3_re),
    .CLK_R(and_6_out), .CLK_F(and_5_out), .S_Int(activationmodule_3_we_f), .IV_OINT_In(16'h3ffe),
    .IV_IO_In(16'h3ffc), .IV_T1_In(16'h3ffa), .IV_T2_In(16'h3ff8), .IP_In(register_file_1_ip_out),
    .FLAG_In({register_file_1_flag_out, register_file_1_flag_out_2}));  // open: T2_Int_In, T1_Int_In, IO_Int_In
  Dual_Register dual_register_1 (
    .D_H_Out(dual_register_1_d_l_out[31:16]), .D_L_Out(dual_register_1_d_l_out[15:0]),
    .CLK_R(activationmodule_4_we_r), .WE_F(activationmodule_4_we_f), .Sup(1'b1),
    .HL(activationmodule_4_mode_w[0]), .Data_In(activationmodule_4_from_bus));
  Instruction_Decoder instruction_decoder_1 (
    .Const_Out(instruction_decoder_1_const_out), .Reg_Sel_A(instruction_decoder_1_reg_sel_a),
    .Const_Reg(instruction_decoder_1_const_reg), .out_14(instruction_decoder_1_out_14),
    .Reg_Sel_In(instruction_decoder_1_reg_sel_in), .Reg_Sel_B(instruction_decoder_1_reg_sel_b),
    .WE1_Out(instruction_decoder_1_we1_out), .WE2_Out(instruction_decoder_1_we2_out),
    .RE1_Out(instruction_decoder_1_re1_out), .RE2_Out(instruction_decoder_1_re2_out),
    .R_Sup(instruction_decoder_1_r_sup), .Zero_One(instruction_decoder_1_zero_one),
    .Reg_Inc(instruction_decoder_1_reg_inc), .Ins_L_In(dual_register_1_d_l_out[31:16]),
    .Ins_H_In(dual_register_1_d_l_out[15:0]), .CLK_R(and_4_out), .CLK_F(and_1_out));
  // Probe on instruction_decoder_1_out_14
  Register #(.width(7)) register_1 (
    .D(activationmodule_1_bus2_out), .clk(activationmodule_5_we_r), .Q(register_1_q));  // open: en, clr
  Register #(.width(16)) register_2 (
    .D(activationmodule_1_bus1_out), .clk(activationmodule_5_we_r), .Q(register_2_q));  // open: en, clr
  Adder #(.width(16)) adder_1 (.a(alu_1_b_out), .b(alu_1_a_out), .out(adder_1_out), .cout(not_8_out[4]));  // open: cin
  Subtractor #(.width(16)) subtractor_1 (.a(alu_1_b_out), .b(alu_1_a_out), .out(subtractor_1_out));  // open: bin, bout
  assign xor_1_out = alu_1_b_out ^ alu_1_a_out;  // XOR_Gate xor_1, 16 bits wide
  assign and_7_out = alu_1_b_out & alu_1_a_out;  // AND_Gate and_7, 16 bits wide
  assign controlled_buffer_1_out = not_7_out ? alu_1_b_out : 16'bz;  // Controlled_Buffer controlled_buffer_1
  not not_7 (not_7_out, register_file_1_flag_out_2[0]);
  assign controlled_buffer_1_out = register_file_1_flag_out_2[0] ? alu_1_a_out : 16'bz;  // Controlled_Buffer controlled_buffer_2
  Comparator #(.width(16)) comparator_1 (
    .a(alu_1_b_out), .b(alu_1_a_out), .gt(not_8_out[2]), .eq(not_8_out[3]), .lt(not_8_out[1]));
  not not_8 (not_8_out[0], not_8_out[3]);
  Register #(.width(16)) register_3 (.D(register_2_q), .clk(activationmodule_5_we_f));  // open: en, Q, clr
  // Probe on instruction_decoder_1_reg_sel_in
  Memory memory_1 (
    .D_Out(memory_1_d_out), .CLK_R(and_6_out), .Sup_In(1'b1), .A_In(activationmodule_1_bus1_out),
    .D_In({activationmodule_1_bus2_out_2, activationmodule_1_bus2_out}), .WE_In(activationmodule_2_we),
    .RE_In(activationmodule_2_re), .WE_F_In(activationmodule_2_we_f));  // open: RE_Out, WE_F_Out, A_Bank_Out, D_Bank_Out, D_Bank_In
  TTY tty_1 (.data(register_1_q), .clk(and_8_out));  // open: we, clr
  and and_8 (and_8_out, activationmodule_5_we_f, activationmodule_5_mode_w[0]);
  // Probe on instruction_decoder_1_reg_sel_a
  // Probe on instruction_decoder_1_reg_sel_b
  // Probe on {register_file_1_flag_out, register_file_1_flag_out_2}
  // Probe on register_file_1_ip_out
  // Probe on 1'b1
  // Probe on dual_register_1_d_l_out

  // Notes on the sheet:
  //   CLK_F
  //   CLK_R
endmodule

module Dual_Register (
  input  [15:0] Data_In,
  input  CLK_R,
  input  WE_F,
  input  Sup,
  input  HL,
  output [15:0] D_H_Out,
  output [15:0] D_L_Out
);

  wire and_1_out, and_2_out, and_3_out, not_1_out;
  wire [15:0] register_1_q;

  not not_1 (not_1_out, HL);
  Register #(.trigger("high"), .width(16)) register_1 (
    .D(Data_In), .en(CLK_R), .clk(CLK_R), .Q(register_1_q));  // open: clr
  and and_1 (and_1_out, WE_F, Sup);
  and and_2 (and_2_out, and_1_out, HL);
  and and_3 (and_3_out, and_1_out, not_1_out);
  Register #(.trigger("high"), .width(16)) register_2 (
    .D(register_1_q), .en(and_3_out), .clk(and_3_out), .Q(D_H_Out));  // open: clr
  Register #(.trigger("high"), .width(16)) register_3 (
    .D(register_1_q), .en(and_2_out), .clk(and_2_out), .Q(D_L_Out));  // open: clr
endmodule

module ALU (
  input  [6:0] Q1_Sel,
  input  [15:0] A_In,
  input  [15:0] B_In,
  input  [15:0] op2,
  input  [15:0] op3,
  input  [15:0] op4,
  input  [15:0] op5,
  input  [15:0] op6,
  input  [15:0] op7,
  input  [6:0] Q2_Sel,
  input  [3:0] Pattern_R,
  output [15:0] A_Out,
  output [15:0] B_Out,
  output [15:0] Q1_Out,
  output [15:0] Q2_Out
);

  wire decoder_1_out0, decoder_1_out1, decoder_1_out2, decoder_1_out3, decoder_1_out4, decoder_1_out5,
       decoder_1_out6, decoder_1_out7, decoder_2_out0, decoder_2_out1, decoder_2_out2, decoder_2_out3,
       decoder_2_out4, decoder_2_out5, decoder_2_out6, decoder_2_out7, nor_1_out, nor_2_out;
  wire [3:0] xor_1_out, xor_2_out;

  assign xor_1_out = Pattern_R ^ Q1_Sel[6:3];  // XOR_Gate xor_1, 4 bits wide
  assign xor_2_out = Q2_Sel[6:3] ^ Pattern_R;  // XOR_Gate xor_2, 4 bits wide
  nor nor_1 (nor_1_out, xor_1_out[0], xor_1_out[1], xor_1_out[2], xor_1_out[3]);
  Decoder #(.select(3)) decoder_1 (
    .out0(decoder_1_out0), .out1(decoder_1_out1), .out2(decoder_1_out2), .out3(decoder_1_out3),
    .out4(decoder_1_out4), .out5(decoder_1_out5), .out6(decoder_1_out6), .out7(decoder_1_out7),
    .sel(Q1_Sel[2:0]), .en(nor_1_out));
  assign Q1_Out = decoder_1_out0 ? A_In : 16'bz;  // Controlled_Buffer controlled_buffer_1
  assign Q2_Out = decoder_2_out0 ? A_In : 16'bz;  // Controlled_Buffer controlled_buffer_2
  Decoder #(.select(3)) decoder_2 (
    .out0(decoder_2_out0), .out1(decoder_2_out1), .out2(decoder_2_out2), .out3(decoder_2_out3),
    .out4(decoder_2_out4), .out5(decoder_2_out5), .out6(decoder_2_out6), .out7(decoder_2_out7),
    .sel(Q2_Sel[2:0]), .en(nor_2_out));
  nor nor_2 (nor_2_out, xor_2_out[0], xor_2_out[1], xor_2_out[2], xor_2_out[3]);
  assign Q1_Out = decoder_1_out1 ? B_In : 16'bz;  // Controlled_Buffer controlled_buffer_3
  assign Q1_Out = decoder_1_out2 ? op2 : 16'bz;  // Controlled_Buffer controlled_buffer_4
  assign Q1_Out = decoder_1_out3 ? op3 : 16'bz;  // Controlled_Buffer controlled_buffer_5
  assign Q1_Out = decoder_1_out4 ? op4 : 16'bz;  // Controlled_Buffer controlled_buffer_6
  assign Q1_Out = decoder_1_out5 ? op5 : 16'bz;  // Controlled_Buffer controlled_buffer_7
  assign Q1_Out = decoder_1_out6 ? op6 : 16'bz;  // Controlled_Buffer controlled_buffer_8
  assign Q1_Out = decoder_1_out7 ? op7 : 16'bz;  // Controlled_Buffer controlled_buffer_9
  assign Q2_Out = decoder_2_out7 ? op7 : 16'bz;  // Controlled_Buffer controlled_buffer_10
  assign Q2_Out = decoder_2_out6 ? op6 : 16'bz;  // Controlled_Buffer controlled_buffer_11
  assign Q2_Out = decoder_2_out5 ? op5 : 16'bz;  // Controlled_Buffer controlled_buffer_12
  assign Q2_Out = decoder_2_out4 ? op4 : 16'bz;  // Controlled_Buffer controlled_buffer_13
  assign Q2_Out = decoder_2_out3 ? op3 : 16'bz;  // Controlled_Buffer controlled_buffer_14
  assign Q2_Out = decoder_2_out2 ? op2 : 16'bz;  // Controlled_Buffer controlled_buffer_15
  assign Q2_Out = decoder_2_out1 ? B_In : 16'bz;  // Controlled_Buffer controlled_buffer_16

  assign A_Out = A_In;
  assign B_Out = B_In;
endmodule

module Instruction_Decoder (
  input  [15:0] Ins_L_In,
  input  [15:0] Ins_H_In,
  input  CLK_R,
  input  CLK_F,
  output Const_Reg,
  output [2:0] Reg_Sel_In,
  output [2:0] Reg_Sel_B,
  output [2:0] Reg_Sel_A,
  output [15:0] Const_Out,
  output [6:0] WE1_Out,
  output [6:0] WE2_Out,
  output [6:0] RE1_Out,
  output [6:0] RE2_Out,
  output [1:0] out_14,
  output R_Sup,
  output Zero_One,
  output Reg_Inc
);

  wire not_1_out, not_2_out, not_3_out;
  wire [1:0] adder_1_out;
  wire [5:0] register_2_q;
  wire [7:0] register_1_q;
  wire [7:2] rom_5_data;

  and and_1 (Const_Reg, Ins_L_In[6], not_1_out);
  not not_1 (not_1_out, rom_5_data[2]);
  Adder #(.width(2)) adder_1 (.a(2'b01), .b(out_14), .out(adder_1_out));  // open: cin, cout
  Register #(.trigger("high")) register_1 (
    .D({Ins_L_In[5:0], adder_1_out}), .clk(CLK_R), .Q(register_1_q));  // open: en, clr
  not not_2 (not_2_out, rom_5_data[2]);
  assign Reg_Sel_In = not_2_out ? Ins_L_In[9:7] : 3'bz;  // Controlled_Buffer controlled_buffer_1
  Register #(.trigger("high")) register_2 (.D(register_1_q), .clk(CLK_F), .Q({register_2_q, out_14}));  // open: en, clr
  assign Reg_Sel_In = rom_5_data[2] ? 3'b001 : 3'bz;  // Controlled_Buffer controlled_buffer_2
  // Probe on {register_2_q, out_14}
  ROM #(.dataWidth(7), .misaligned("true")) rom_1 (.addr({register_2_q, out_14}), .data(WE1_Out));
  ROM #(.dataWidth(7), .misaligned("true")) rom_2 (.addr({register_2_q, out_14}), .data(WE2_Out));
  ROM #(.dataWidth(7), .misaligned("true")) rom_3 (.addr({register_2_q, out_14}), .data(RE1_Out));
  ROM #(.dataWidth(7), .misaligned("true")) rom_4 (.addr({register_2_q, out_14}), .data(RE2_Out));
  ROM #(.misaligned("true")) rom_5 (
    .addr({register_2_q, out_14}), .data({rom_5_data[7:4], Reg_Inc, rom_5_data[2], Zero_One, R_Sup}));
  assign Reg_Sel_B = rom_5_data[2] ? 3'b001 : 3'bz;  // Controlled_Buffer controlled_buffer_3
  not not_3 (not_3_out, rom_5_data[2]);
  assign Reg_Sel_B = not_3_out ? Ins_L_In[15:13] : 3'bz;  // Controlled_Buffer controlled_buffer_4

  assign Const_Out = Ins_H_In;
  assign Reg_Sel_A = Ins_L_In[12:10];

  // Notes on the sheet:
  //   contents of rom_1 (hex, n*v repeats v):
  //   8 8 0 0 8 8 8 0 8 8 8 0 8 8 8 0 8 8 0 0 8 8 0 0 8 8 8 0 8 8 8 0 8 8 0 0 8 8 0 0 8 8 10 0 8 8 0 0 8 8
  //   0 0 8 8 0 0 8 8 0 0 8 8 0 0 8 8 0 0 8 8 0 0 8 8 8 0 8 8 8 0 8 8 0 0 8 8 0 0 8 8 0 0 8 8 0 0 8 8 0 0
  //   8 8 0 0 8 8 30 0 8 8 31 0 8 8 0 0 8 8 0 0 8 8 0 0 8 8 0 0 8 8 0 0 8 8 0 0 8 8 0 0 8 8 0 0 8 8 0 0 8
  //   8 0 0 8 8 0 0 8 8 0 0 8 8 0 0 8 8 0 0 8 8 0 0 8 8 0 0 8 8 0 0 8 8 0 0 8 8 0 0 8 8 0 0 8 8 0 0 8 8 0
  //   0 8 8 0 0 8 8 0 0 8 8 0 0 8 8 0 0 8 8 0 0 8 8 0 0 8 8 0 0 8 8 0 0 8 8 0 0 8 8 0 0 8 8 0 0 8 8 0 0 8
  //   8 0 0 8 8
  //   contents of rom_2 (hex, n*v repeats v):
  //   29 28 0 0 29 28 0 0 29 28 0 0 29 28 0 0 29 28 0 0 29 28 0 0 29 28 0 0 29 28 0 0 29 28 0 0 29 28 0 0
  //   29 28 0 0 29 28 8 0 29 28 0 0 29 28 0 0 29 28 0 0 29 28 0 0 29 28 0 0 29 28 0 0 29 28 0 0 29 28 0 0
  //   29 28 0 0 29 28 0 0 29 28 0 0 29 28 0 0 29 28 0 0 29 28 0 0 29 28 0 0 29 28 0 0 29 28 0 0 29 28 0 0
  //   29 28 0 0 29 28 0 0 29 28 0 0 29 28 0 0 29 28 0 0 29 28 0 0 29 28 0 0 29 28 0 0 29 28 0 0 29 28 0 0
  //   29 28 0 0 29 28 0 0 29 28 0 0 29 28 0 0 29 28 0 0 29 28 0 0 29 28 0 0 29 28 0 0 29 28 0 0 29 28 0 0
  //   29 28 0 0 29 28 0 0 29 28 0 0 29 28 0 0 29 28 0 0 29 28 0 0 29 28 0 0 29 28 0 0 29 28 0 0 29 28 0 0
  //   29 28 0 0 29 28 0 0 29 28 0 0 29 28
  //   contents of rom_3 (hex, n*v repeats v):
  //   20 9 0 0 20 9 9 0 20 9 a 0 20 9 b 0 20 9 0 0 20 9 0 0 20 9 c 0 20 9 d 0 20 9 0 0 20 9 0 0 20 9 a 0
  //   20 9 a 0 20 9 0 0 20 9 0 0 20 9 0 0 20 9 0 0 20 9 0 0 20 9 0 0 20 9 f 0 20 9 e 0 20 9 0 0 20 9 0 0
  //   20 9 0 0 20 9 0 0 20 9 0 0 20 9 0 0 20 9 8 0 20 9 8 0 20 9 0 0 20 9 0 0 20 9 0 0 20 9 0 0 20 9 0 0
  //   20 9 0 0 20 9 0 0 20 9 0 0 20 9 0 0 20 9 0 0 20 9 0 0 20 9 0 0 20 9 0 0 20 9 0 0 20 9 0 0 20 9 0 0
  //   20 9 0 0 20 9 0 0 20 9 0 0 20 9 0 0 20 9 0 0 20 9 0 0 20 9 0 0 20 9 0 0 20 9 0 0 20 9 0 0 20 9 0 0
  //   20 9 0 0 20 9 0 0 20 9 0 0 20 9 0 0 20 9 0 0 20 9 0 0 20 9 0 0 20 9 0 0 20 9
  //   contents of rom_4 (hex, n*v repeats v):
  //   10 10 0 0 10 10 0 0 10 10 0 0 10 10 0 0 10 10 0 0 10 10 0 0 10 10 0 0 10 10 0 0 10 10 0 0 10 10 0 0
  //   10 10 9 0 10 10 10 0 10 10 0 0 10 10 0 0 10 10 0 0 10 10 0 0 10 10 0 0 10 10 0 0 10 10 0 0 10 10 0 0
  //   10 10 0 0 10 10 0 0 10 10 0 0 10 10 0 0 10 10 0 0 10 10 0 0 10 10 9 0 10 10 9 0 10 10 0 0 10 10 0 0
  //   10 10 0 0 10 10 0 0 10 10 0 0 10 10 0 0 10 10 0 0 10 10 0 0 10 10 0 0 10 10 0 0 10 10 0 0 10 10 0 0
  //   10 10 0 0 10 10 0 0 10 10 0 0 10 10 0 0 10 10 0 0 10 10 0 0 10 10 0 0 10 10 0 0 10 10 0 0 10 10 0 0
  //   10 10 0 0 10 10 0 0 10 10 0 0 10 10 0 0 10 10 0 0 10 10 0 0 10 10 0 0 10 10 0 0 10 10 0 0 10 10 0 0
  //   10 10 0 0 10 10 0 0 10 10 0 0 10 10
  //   contents of rom_5 (hex, n*v repeats v):
  //   c c 0 0 c c 0 0 c c 0 0 c c 0 0 c c 0 0 c c 0 0 c c 0 0 c c 0 0 c c 0 0 c c 0 0 c c 0 0 c c 0 0 c c
  //   0 0 c c 0 0 c c 0 0 c c 0 0 c c 0 0 c c 0 0 c c 0 0 c c 0 0 c c 0 0 c c 0 0 c c 0 0 c c 0 0 c c 0 0
  //   c c 0 0 c c 0 0 c c 0 0 c c 0 0 c c 0 0 c c 0 0 c c 0 0 c c 0 0 c c 0 0 c c 0 0 c c 0 0 c c 0 0 c c
  //   0 0 c c 0 0 c c 0 0 c c 0 0 c c 0 0 c c 0 0 c c 0 0 c c 0 0 c c 0 0 c c 0 0 c c 0 0 c c 0 0 c c 0 0
  //   c c 0 0 c c 0 0 c c 0 0 c c 0 0 c c 0 0 c c 0 0 c c 0 0 c c 0 0 c c 0 0 c c 0 0 c c 0 0 c c 0 0 c c
  //   0 0 c c
endmodule

module Interrupt_Controller (
  input  T2_Int_In,
  input  T1_Int_In,
  input  IO_Int_In,
  input  S_Int,
  input  CLK_R,
  input  CLK_F,
  input  [15:0] FLAG_In,
  input  RE,
  input  [15:0] IV_OINT_In,
  input  [15:0] IV_IO_In,
  input  [15:0] IV_T1_In,
  input  [15:0] IV_T2_In,
  input  [15:0] IP_In,
  output S_Sup,
  output [15:0] IP_Out
);

  wire and_1_out, and_2_out, and_4_out, and_5_out, and_6_out, and_7_out, and_8_out, and_9_out, and_10_out,
       and_11_out, and_12_out, d_ff_1_q, d_ff_2_q, d_ff_3_q, d_ff_4_q, d_ff_5_q, d_ff_6_q, d_ff_7_q,
       d_ff_8_q, d_ff_9_q, d_ff_10_q, d_ff_11_q, d_ff_12_q, not_1_out, not_2_out, not_3_out, not_4_out,
       not_5_out, not_6_out, not_7_out, or_1_out, or_2_out, or_3_out, undriven;

  and and_1 (and_1_out, undriven, or_2_out);
  D_Flip_Flop d_ff_1 (.Q(d_ff_1_q), .preset(S_Int), .reset(d_ff_2_q));  // open: D, clk, Qn
  D_Flip_Flop d_ff_2 (.D(d_ff_3_q), .clk(CLK_R), .Q(d_ff_2_q));  // open: Qn, preset, reset
  D_Flip_Flop d_ff_3 (.D(d_ff_1_q), .clk(and_2_out), .Q(d_ff_3_q));  // open: Qn, preset, reset
  and and_2 (and_2_out, CLK_F, undriven);
  and and_3 (S_Sup, CLK_R, and_1_out);
  or or_1 (or_1_out, d_ff_1_q, and_5_out);
  or or_2 (or_2_out, or_1_out, or_3_out);
  or or_3 (or_3_out, and_7_out, and_9_out);
  not not_1 (not_1_out, or_2_out);
  D_Flip_Flop d_ff_4 (.Q(d_ff_4_q), .preset(IO_Int_In), .reset(d_ff_5_q));  // open: D, clk, Qn
  D_Flip_Flop d_ff_5 (.D(d_ff_6_q), .clk(CLK_R), .Q(d_ff_5_q));  // open: Qn, preset, reset
  D_Flip_Flop d_ff_6 (.D(and_5_out), .clk(and_2_out), .Q(d_ff_6_q));  // open: Qn, preset, reset
  not not_2 (not_2_out, d_ff_1_q);
  assign IP_Out = d_ff_1_q ? IV_OINT_In : 16'bz;  // Controlled_Buffer controlled_buffer_1
  and and_4 (and_4_out, d_ff_4_q, not_7_out);
  and and_5 (and_5_out, not_2_out, and_4_out);
  assign IP_Out = and_5_out ? IV_IO_In : 16'bz;  // Controlled_Buffer controlled_buffer_2
  D_Flip_Flop d_ff_7 (.Q(d_ff_7_q), .preset(T1_Int_In), .reset(d_ff_8_q));  // open: D, clk, Qn
  D_Flip_Flop d_ff_8 (.D(d_ff_9_q), .clk(CLK_R), .Q(d_ff_8_q));  // open: Qn, preset, reset
  D_Flip_Flop d_ff_9 (.D(and_7_out), .clk(and_2_out), .Q(d_ff_9_q));  // open: Qn, preset, reset
  and and_6 (and_6_out, not_2_out, and_8_out);
  not not_3 (not_3_out, and_5_out);
  and and_7 (and_7_out, not_3_out, and_6_out);
  assign IP_Out = and_7_out ? IV_T1_In : 16'bz;  // Controlled_Buffer controlled_buffer_3
  D_Flip_Flop d_ff_10 (.Q(d_ff_10_q), .preset(T2_Int_In), .reset(d_ff_11_q));  // open: D, clk, Qn
  D_Flip_Flop d_ff_11 (.D(d_ff_12_q), .clk(CLK_R), .Q(d_ff_11_q));  // open: Qn, preset, reset
  D_Flip_Flop d_ff_12 (.D(and_9_out), .clk(and_2_out), .Q(d_ff_12_q));  // open: Qn, preset, reset
  and and_8 (and_8_out, d_ff_7_q, not_5_out);
  not not_4 (not_4_out, and_7_out);
  and and_9 (and_9_out, not_4_out, and_12_out);
  not not_5 (not_5_out, FLAG_In[8]);
  not not_6 (not_6_out, FLAG_In[9]);
  not not_7 (not_7_out, FLAG_In[10]);
  and and_10 (and_10_out, d_ff_10_q, not_6_out);
  and and_11 (and_11_out, not_2_out, and_10_out);
  and and_12 (and_12_out, not_3_out, and_11_out);
  assign IP_Out = and_9_out ? IV_T2_In : 16'bz;  // Controlled_Buffer controlled_buffer_4
  assign IP_Out = not_1_out ? IP_In : 16'bz;  // Controlled_Buffer controlled_buffer_5
endmodule

module Bank_Controller (
  input  [15:0] D_Mem_In,
  input  [15:0] D_Bank_In,
  input  [15:0] A_In,
  input  RE_In,
  input  WE_In,
  input  [15:0] ID1_In,
  input  [15:0] ID2_In,
  output [7:0] Pattern_Out,
  output [15:0] D_Bank_Out,
  output [15:0] D_Mem_Out,
  output [13:0] A_Out,
  output OE_Out,
  output WE_Out,
  output [7:0] ID_Out
);

  wire not_1_out, not_2_out;

  and and_1 (OE_Out, A_In[15], RE_In);
  and and_2 (WE_Out, A_In[15], WE_In);
  not not_1 (not_1_out, A_In[14]);
  assign ID_Out = not_1_out ? ID1_In[7:0] : 8'bz;  // Controlled_Buffer controlled_buffer_1
  not not_2 (not_2_out, not_1_out);
  assign ID_Out = not_2_out ? ID2_In[7:0] : 8'bz;  // Controlled_Buffer controlled_buffer_2

  assign A_Out = A_In[13:0];
  assign D_Bank_Out = D_Mem_In;
  assign D_Mem_Out = D_Bank_In;
  assign Pattern_Out = {8{1'b0}};
endmodule

module Bank_Module_x4 (
  input  [13:0] Addr_In,
  input  [7:0] Pattern_In,
  input  [15:0] D_In,
  input  [7:0] ID_In,
  input  OE_In,
  input  WE_In,
  output [7:0] Pattern_Out,
  output [13:0] Addr_Out,
  output [15:0] D_Out,
  output [7:0] ID_Out,
  output OE_Out,
  output WE_Out
);

  wire nand_1_out, nand_2_out, nor_1_out, not_1_out, not_2_out;
  wire [7:0] xor_1_out;
  wire [15:0] ram_1_dout;

  Hex_Digit_Display hex_digit_display_1 (.value(Pattern_In[7:4]));  // open: dp
  Hex_Digit_Display hex_digit_display_2 (.value(Pattern_In[3:0]));  // open: dp
  Adder adder_1 (.a(8'h4), .b(Pattern_In), .out(Pattern_Out));  // open: cin, cout
  assign xor_1_out = Pattern_In ^ ID_In;  // XOR_Gate xor_1, 8 bits wide
  LED led_1 (.in(nor_1_out));
  nor nor_1 (nor_1_out, xor_1_out[2], xor_1_out[3], xor_1_out[4], xor_1_out[5], xor_1_out[6], xor_1_out[7]);
  nand nand_1 (nand_1_out, nor_1_out, WE_In);
  nand nand_2 (nand_2_out, nor_1_out, OE_In);
  not not_1 (not_1_out, nand_1_out);
  not not_2 (not_2_out, nand_2_out);
  RAM #(.addrWidth(16), .dataWidth(16), .trigger("high")) ram_1 (
    .addr({ID_In[1:0], Addr_In}), .we(not_1_out), .oe(not_2_out), .din(D_In), .dout(ram_1_dout));
  assign D_Out = not_2_out ? ram_1_dout : 16'bz;  // Controlled_Buffer controlled_buffer_1

  assign Addr_Out = Addr_In;
  assign ID_Out = ID_In;
  assign OE_Out = OE_In;
  assign WE_Out = WE_In;
endmodule

module Bank_Module_x2 (
  input  [13:0] Addr_In,
  input  [7:0] Pattern_In,
  input  [15:0] D_In,
  input  [7:0] ID_In,
  input  OE_In,
  input  WE_In,
  output [7:0] Pattern_Out,
  output [13:0] Addr_Out,
  output [15:0] D_Out,
  output [7:0] ID_Out,
  output OE_Out,
  output WE_Out
);

  wire nand_1_out, nand_2_out, nor_1_out, not_1_out, not_2_out;
  wire [7:0] xor_1_out;
  wire [15:0] ram_1_dout;

  Hex_Digit_Display hex_digit_display_1 (.value(Pattern_In[7:4]));  // open: dp
  Hex_Digit_Display hex_digit_display_2 (.value(Pattern_In[3:0]));  // open: dp
  Adder adder_1 (.a(8'h2), .b(Pattern_In), .out(Pattern_Out));  // open: cin, cout
  assign xor_1_out = Pattern_In ^ ID_In;  // XOR_Gate xor_1, 8 bits wide
  nor nor_1 (nor_1_out, xor_1_out[1], xor_1_out[2], xor_1_out[3], xor_1_out[4], xor_1_out[5], xor_1_out[6], xor_1_out[7]);
  LED led_1 (.in(nor_1_out));
  nand nand_1 (nand_1_out, nor_1_out, WE_In);
  nand nand_2 (nand_2_out, nor_1_out, OE_In);
  not not_1 (not_1_out, nand_1_out);
  not not_2 (not_2_out, nand_2_out);
  RAM #(.addrWidth(15), .dataWidth(16), .trigger("high")) ram_1 (
    .addr({ID_In[0], Addr_In}), .we(not_1_out), .oe(not_2_out), .din(D_In), .dout(ram_1_dout));
  assign D_Out = not_2_out ? ram_1_dout : 16'bz;  // Controlled_Buffer controlled_buffer_1

  assign Addr_Out = Addr_In;
  assign ID_Out = ID_In;
  assign OE_Out = OE_In;
  assign WE_Out = WE_In;
endmodule

module Memory (
  input  [15:0] D_In,
  input  CLK_R,
  input  Sup_In,
  input  [15:0] A_In,
  input  [15:0] D_Bank_In,
  input  WE_In,
  input  RE_In,
  input  WE_F_In,
  output [15:0] D_Out,
  output [15:0] A_Bank_Out,
  output [15:0] D_Bank_Out,
  output RE_Out,
  output WE_F_Out
);

  wire and_1_out, and_2_out, and_3_out, decoder_1_out0, decoder_1_out1, not_1_out, not_2_out, not_3_out,
       not_4_out;
  wire [15:0] register_1_q, rom_1_data;

  Register #(.trigger("high"), .width(16)) register_1 (
    .D(D_In), .en(CLK_R), .clk(CLK_R), .Q(register_1_q));  // open: clr
  Decoder #(.select(2)) decoder_1 (
    .out0(decoder_1_out0), .out1(decoder_1_out1), .sel(A_In[15:14]), .en(Sup_In));  // open: out2, out3
  not not_1 (not_1_out, decoder_1_out0);
  not not_2 (not_2_out, decoder_1_out1);
  not not_3 (not_3_out, not_1_out);
  not not_4 (not_4_out, not_2_out);
  and and_1 (and_1_out, not_3_out, RE_In);
  and and_2 (and_2_out, not_4_out, RE_In);
  and and_3 (and_3_out, not_4_out, WE_F_In);
  assign D_Bank_In = WE_In ? register_1_q : 16'bz;  // Controlled_Buffer controlled_buffer_1
  RAM #(.addrWidth(14), .dataWidth(16), .databus("bidir"), .enables("line"), .trigger("high"), .\type ("nonvolatile")) ram_1 (
    .addr(A_In[13:0]), .we(and_3_out), .oe(and_2_out), .clk(and_3_out), .data(D_Bank_In));
  ROM #(.addrWidth(14), .dataWidth(16)) rom_1 (.addr(A_In[13:0]), .data(rom_1_data));
  assign D_Bank_In = and_1_out ? rom_1_data : 16'bz;  // Controlled_Buffer controlled_buffer_2

  assign A_Bank_Out = A_In;
  assign D_Bank_Out = D_Bank_In;
  assign D_Out = D_Bank_In;
  assign RE_Out = RE_In;
  assign WE_F_Out = WE_F_In;

  // Notes on the sheet:
  //   contents of rom_1 (hex, n*v repeats v):
  //   14 c1 54 68 65 20 61 6e 73 77 65 72 20 69 73 20 34 32 21 0 0 181 1337 241 f 105a 3c 105a 1 105a 2
  //   105a 2 ecb 1 dc2 0 17d2 2c 4d3 0 b01b 20 c1 ffff ffff 2c c1
endmodule

module Register_File (
  input  R_Sup,
  input  S_Sup,
  input  Zero_One,
  input  Inc,
  input  [15:0] D_In,
  input  CLK_R,
  input  CLK_F,
  input  WE,
  input  [2:0] D_Sel,
  input  [2:0] A_Sel,
  input  [15:0] Const_In,
  input  Const_Reg,
  input  [2:0] B_Sel,
  output Sup_Out,
  output [15:0] A_Out,
  output [15:0] B_Out,
  output [15:0] IP_Out,
  output [15:0] FLAG_Out
);

  wire and_1_out, and_2_out, and_3_out, and_4_out, and_5_out, and_6_out, and_7_out, and_8_out, and_9_out,
       and_10_out, and_11_out, and_12_out, decoder_1_out1, decoder_1_out2, decoder_1_out3, decoder_1_out4,
       decoder_1_out5, decoder_1_out6, decoder_1_out7, decoder_2_out0, decoder_2_out1, decoder_2_out2,
       decoder_2_out3, decoder_2_out4, decoder_2_out5, decoder_2_out6, decoder_2_out7, decoder_3_out0,
       decoder_3_out1, decoder_3_out2, decoder_3_out3, decoder_3_out4, decoder_3_out5, decoder_3_out6,
       decoder_3_out7, not_1_out, not_2_out, or_1_out, or_2_out;
  wire [7:0] register_1_q, register_1_q_2;
  wire [15:0] A_q, adder_1_out, B_q, C_q, D_q, SP_q;

  Adder #(.width(16)) adder_1 (.a({{15{1'b0}}, Inc}), .b(D_In), .out(adder_1_out));  // open: cin, cout
  and and_1 (and_1_out, CLK_R, WE);
  and and_2 (and_2_out, CLK_F, WE);
  Decoder #(.select(3)) decoder_1 (
    .out1(decoder_1_out1), .out2(decoder_1_out2), .out3(decoder_1_out3), .out4(decoder_1_out4),
    .out5(decoder_1_out5), .out6(decoder_1_out6), .out7(decoder_1_out7), .sel(D_Sel));  // open: out0, en
  Decoder #(.select(3)) decoder_2 (
    .out0(decoder_2_out0), .out1(decoder_2_out1), .out2(decoder_2_out2), .out3(decoder_2_out3),
    .out4(decoder_2_out4), .out5(decoder_2_out5), .out6(decoder_2_out6), .out7(decoder_2_out7), .sel(A_Sel));  // open: en
  Decoder #(.select(3)) decoder_3 (
    .out0(decoder_3_out0), .out1(decoder_3_out1), .out2(decoder_3_out2), .out3(decoder_3_out3),
    .out4(decoder_3_out4), .out5(decoder_3_out5), .out6(decoder_3_out6), .out7(decoder_3_out7), .sel(B_Sel),
    .en(not_2_out));
  Register #(.trigger("high"), .width(16)) register_1 (
    .D(adder_1_out), .clk(and_1_out), .Q({register_1_q_2, register_1_q}));  // open: en, clr
  assign A_Out = decoder_2_out0 ? {{15{1'b0}}, Zero_One} : 16'bz;  // Controlled_Buffer controlled_buffer_1
  assign B_Out = decoder_3_out0 ? {{15{1'b0}}, Zero_One} : 16'bz;  // Controlled_Buffer controlled_buffer_2
  Register #(.trigger("high"), .width(16)) IP (
    .D({register_1_q_2, register_1_q}), .clk(and_3_out), .Q(IP_Out));  // open: en, clr
  and and_3 (and_3_out, and_2_out, decoder_1_out1);
  Register #(.trigger("high"), .width(16)) SP (
    .D({register_1_q_2, register_1_q}), .clk(and_4_out), .Q(SP_q));  // open: en, clr
  and and_4 (and_4_out, and_2_out, decoder_1_out2);
  assign A_Out = decoder_2_out1 ? IP_Out : 16'bz;  // Controlled_Buffer controlled_buffer_3
  assign B_Out = decoder_3_out1 ? IP_Out : 16'bz;  // Controlled_Buffer controlled_buffer_4
  assign A_Out = decoder_2_out2 ? SP_q : 16'bz;  // Controlled_Buffer controlled_buffer_5
  assign B_Out = decoder_3_out2 ? SP_q : 16'bz;  // Controlled_Buffer controlled_buffer_6
  Register #(.trigger("high"), .width(16)) A (
    .D({register_1_q_2, register_1_q}), .clk(and_5_out), .Q(A_q));  // open: en, clr
  and and_5 (and_5_out, and_2_out, decoder_1_out3);
  assign A_Out = decoder_2_out3 ? A_q : 16'bz;  // Controlled_Buffer controlled_buffer_7
  assign B_Out = decoder_3_out3 ? A_q : 16'bz;  // Controlled_Buffer controlled_buffer_8
  Register #(.trigger("high"), .width(16)) B (
    .D({register_1_q_2, register_1_q}), .clk(and_6_out), .Q(B_q));  // open: en, clr
  and and_6 (and_6_out, and_2_out, decoder_1_out4);
  Register #(.trigger("high"), .width(16)) C (
    .D({register_1_q_2, register_1_q}), .clk(and_7_out), .Q(C_q));  // open: en, clr
  and and_7 (and_7_out, and_2_out, decoder_1_out5);
  assign A_Out = decoder_2_out4 ? B_q : 16'bz;  // Controlled_Buffer controlled_buffer_9
  assign B_Out = decoder_3_out4 ? B_q : 16'bz;  // Controlled_Buffer controlled_buffer_10
  assign A_Out = decoder_2_out5 ? C_q : 16'bz;  // Controlled_Buffer controlled_buffer_11
  assign B_Out = decoder_3_out5 ? C_q : 16'bz;  // Controlled_Buffer controlled_buffer_12
  Register #(.trigger("high"), .width(16)) D (
    .D({register_1_q_2, register_1_q}), .clk(and_8_out), .Q(D_q));  // open: en, clr
  and and_8 (and_8_out, and_2_out, decoder_1_out6);
  and and_9 (and_9_out, and_2_out, decoder_1_out7);
  assign A_Out = decoder_2_out6 ? D_q : 16'bz;  // Controlled_Buffer controlled_buffer_13
  assign B_Out = decoder_3_out6 ? D_q : 16'bz;  // Controlled_Buffer controlled_buffer_14
  Register #(.trigger("high")) FLAG_0 (.D(register_1_q), .clk(and_9_out), .Q(FLAG_Out[7:0]));  // open: en, clr
  and and_10 (and_10_out, and_9_out, FLAG_Out[15]);
  not not_1 (not_1_out, register_1_q_2[7]);
  assign A_Out = decoder_2_out7 ? FLAG_Out : 16'bz;  // Controlled_Buffer controlled_buffer_15
  assign B_Out = decoder_3_out7 ? FLAG_Out : 16'bz;  // Controlled_Buffer controlled_buffer_16
  and and_11 (and_11_out, register_1_q_2[7], and_10_out);
  and and_12 (and_12_out, and_10_out, not_1_out);
  Register #(.trigger("high"), .width(7)) FLAG_1 (
    .D(register_1_q_2[6:0]), .clk(and_10_out), .Q(FLAG_Out[14:8]));  // open: en, clr
  or or_1 (or_1_out, S_Sup, and_11_out);
  J_K_Flip_Flop j_k_ff_1 (.Q(FLAG_Out[15]), .preset(or_1_out), .reset(or_2_out));  // open: J, K, clk, Qn
  or or_2 (or_2_out, R_Sup, and_12_out);
  assign B_Out = Const_Reg ? Const_In : 16'bz;  // Controlled_Buffer controlled_buffer_17
  not not_2 (not_2_out, Const_Reg);

  assign Sup_Out = FLAG_Out[15];
endmodule

module main_Timer (
);

  wire and_1_out, and_2_out, clock_1_out, clock_2_out, counter_1_carry, counter_2_carry, j_k_ff_1_q,
       not_1_out, not_2_out, not_3_out;

  Counter #(.max('h3e8), .width(12)) counter_1 (
    .clk(clock_1_out), .carry(counter_1_carry));  // open: clr, load, up, count, D, Q
  Clock clock_1 (.out(clock_1_out));
  Counter #(.max('h32), .width(32)) counter_2 (
    .clk(clock_2_out), .carry(counter_2_carry));  // open: clr, load, up, count, D, Q
  Clock clock_2 (.out(clock_2_out));
  J_K_Flip_Flop j_k_ff_1 (
    .J(counter_2_carry), .K(counter_2_carry), .clk(counter_2_carry), .Q(j_k_ff_1_q));  // open: Qn, preset, reset
  not not_1 (not_1_out, j_k_ff_1_q);
  not not_2 (not_2_out, j_k_ff_1_q);
  and and_1 (and_1_out, not_1_out, j_k_ff_1_q);
  not not_3 (not_3_out, not_2_out);
  and and_2 (and_2_out, not_3_out, not_2_out);
  Freq_Counter freq_counter_1 (.Ref_CLK(counter_1_carry), .CLK_R(and_1_out), .CLK_F(and_2_out));  // open: Freq_Out, HL
endmodule

module Freq_Counter (
  input  Ref_CLK,
  input  HL,
  input  CLK_R,
  input  CLK_F,
  output [15:0] Freq_Out
);

  wire and_1_out, and_2_out, counter_1_carry, not_1_out, not_2_out, not_3_out, not_4_out, not_5_out,
       not_6_out;
  wire [23:0] counter_1_q;
  wire [31:0] register_1_q;

  and and_1 (and_1_out, not_1_out, Ref_CLK);
  and and_2 (and_2_out, not_2_out, not_3_out);
  not not_1 (not_1_out, Ref_CLK);
  not not_2 (not_2_out, not_3_out);
  not not_3 (not_3_out, Ref_CLK);
  Counter #(.max('hffffff), .width(24)) counter_1 (
    .clr(and_2_out), .load(Ref_CLK), .count(1'b1), .clk(CLK_R), .D({24{1'b0}}), .carry(counter_1_carry),
    .Q(counter_1_q));  // open: up
  Register #(.trigger("high"), .width(32)) register_1 (
    .D({{8{1'b0}}, counter_1_q}), .en(and_1_out), .clk(and_1_out), .Q(register_1_q));  // open: clr
  assign Freq_Out = not_4_out ? register_1_q[15:0] : 16'bz;  // Controlled_Buffer controlled_buffer_1
  not not_4 (not_4_out, HL);
  not not_5 (not_5_out, HL);
  assign Freq_Out = not_6_out ? register_1_q[31:16] : 16'bz;  // Controlled_Buffer controlled_buffer_2
  not not_6 (not_6_out, not_5_out);
endmodule

module Timer (
  input  Low_High,
  input  [15:0] D_In,
  input  T1T2,
  input  Sup_In,
  input  WE,
  input  CLK_F,
  input  StopMode,
  input  CLK_Ref,
  input  CLK_R,
  output [15:0] D_Out,
  output T1_Int_Out,
  output T2_Int_Out
);

  wire and_1_out, and_2_out, and_3_out, and_4_out, and_5_out, and_6_out, and_7_out, and_8_out, and_9_out,
       and_10_out, and_11_out, and_12_out, and_14_out, and_15_out, and_16_out, and_17_out, and_18_out,
       decoder_1_out0, decoder_1_out1, decoder_1_out2, decoder_1_out3, decoder_2_out1, decoder_2_out2,
       decoder_2_out3, decoder_3_out1, decoder_3_out2, decoder_3_out3, j_k_ff_1_q, j_k_ff_2_q, nor_1_out,
       nor_2_out, nor_3_out, nor_4_out, nor_5_out, nor_6_out, nor_7_out, nor_8_out, not_1_out, not_2_out,
       not_3_out, not_4_out, not_5_out, not_6_out, not_7_out, not_8_out, not_9_out, not_10_out, not_11_out,
       not_12_out, not_13_out, not_14_out, or_1_out, or_2_out, or_3_out, or_4_out, or_5_out, or_6_out;
  wire [1:0] Mode_T1_q, register_3_q;
  wire [15:0] register_1_q, register_2_q, Stop_T1_H_q, Stop_T1_L_q;
  wire [31:0] counter_1_q, counter_2_q, xor_1_out, xor_2_out;

  and and_1 (and_1_out, Sup_In, WE);
  and and_2 (and_2_out, not_1_out, and_4_out);
  not not_1 (not_1_out, StopMode);
  and and_3 (and_3_out, StopMode, and_4_out);
  and and_4 (and_4_out, and_1_out, CLK_F);
  Freq_Counter freq_counter_1 (.Freq_Out(D_Out), .HL(Low_High), .Ref_CLK(CLK_Ref), .CLK_R(CLK_R), .CLK_F(CLK_F));
  Decoder #(.select(2)) decoder_1 (
    .out0(decoder_1_out0), .out1(decoder_1_out1), .out2(decoder_1_out2), .out3(decoder_1_out3),
    .sel({T1T2, Low_High}), .en(and_2_out));
  not not_2 (not_2_out, T1T2);
  not not_3 (not_3_out, decoder_1_out0);
  not not_4 (not_4_out, decoder_1_out1);
  not not_5 (not_5_out, decoder_1_out2);
  not not_6 (not_6_out, decoder_1_out3);
  not not_7 (not_7_out, Sup_In);
  not not_8 (not_8_out, not_2_out);
  Register #(.width(16)) Stop_T1_L (.D(D_In), .en(not_9_out), .clk(not_9_out), .Q(Stop_T1_L_q));  // open: clr
  not not_9 (not_9_out, not_3_out);
  Register #(.width(16)) Stop_T1_H (.D(D_In), .en(not_10_out), .clk(not_10_out), .Q(Stop_T1_H_q));  // open: clr
  not not_10 (not_10_out, not_4_out);
  and and_5 (and_5_out, not_7_out, Sup_In);
  and and_6 (and_6_out, and_3_out, not_2_out);
  and and_7 (and_7_out, and_3_out, not_8_out);
  Register #(.trigger("high"), .width(2)) Mode_T1 (
    .D(D_In[1:0]), .en(or_1_out), .clk(or_1_out), .Q(Mode_T1_q));  // open: clr
  or or_1 (or_1_out, and_5_out, and_6_out);
  Decoder #(.select(2)) decoder_2 (
    .out1(decoder_2_out1), .out2(decoder_2_out2), .out3(decoder_2_out3), .sel(Mode_T1_q));  // open: out0, en
  not not_11 (not_11_out, decoder_2_out3);
  and and_8 (and_8_out, not_11_out, decoder_2_out3);
  or or_2 (or_2_out, T1_Int_Out, decoder_2_out1);
  and and_9 (and_9_out, or_2_out, CLK_F);
  or or_3 (or_3_out, decoder_2_out2, j_k_ff_1_q);
  and and_10 (and_10_out, or_3_out, CLK_R);
  J_K_Flip_Flop j_k_ff_1 (.Q(j_k_ff_1_q), .preset(and_8_out), .reset(T1_Int_Out));  // open: J, K, clk, Qn
  Counter #(.max('hffffffff), .width(32)) counter_1 (
    .clr(and_9_out), .up(1'b1), .clk(and_10_out), .Q(counter_1_q));  // open: load, count, D, carry
  assign xor_1_out = {Stop_T1_H_q, Stop_T1_L_q} ^ counter_1_q;  // XOR_Gate xor_1, 32 bits wide
  nor nor_1 (nor_1_out, xor_1_out[0], xor_1_out[1], xor_1_out[2], xor_1_out[3], xor_1_out[4], xor_1_out[5], xor_1_out[6], xor_1_out[7]);
  nor nor_2 (nor_2_out, xor_1_out[8], xor_1_out[9], xor_1_out[10], xor_1_out[11], xor_1_out[12], xor_1_out[13], xor_1_out[14], xor_1_out[15]);
  nor nor_3 (nor_3_out, xor_1_out[16], xor_1_out[17], xor_1_out[18], xor_1_out[19], xor_1_out[20], xor_1_out[21], xor_1_out[22], xor_1_out[23]);
  nor nor_4 (nor_4_out, xor_1_out[24], xor_1_out[25], xor_1_out[26], xor_1_out[27], xor_1_out[28], xor_1_out[29], xor_1_out[30], xor_1_out[31]);
  and and_11 (and_11_out, nor_1_out, nor_2_out);
  and and_12 (and_12_out, nor_3_out, nor_4_out);
  Register #(.width(16)) register_1 (.D(D_In), .en(not_12_out), .clk(not_12_out), .Q(register_1_q));  // open: clr
  not not_12 (not_12_out, not_5_out);
  Register #(.width(16)) register_2 (.D(D_In), .en(not_13_out), .clk(not_13_out), .Q(register_2_q));  // open: clr
  not not_13 (not_13_out, not_6_out);
  and and_13 (T1_Int_Out, and_11_out, and_12_out);
  Register #(.trigger("high"), .width(2)) register_3 (
    .D(D_In[1:0]), .en(or_4_out), .clk(or_4_out), .Q(register_3_q));  // open: clr
  or or_4 (or_4_out, and_5_out, and_7_out);
  Decoder #(.select(2)) decoder_3 (
    .out1(decoder_3_out1), .out2(decoder_3_out2), .out3(decoder_3_out3), .sel(register_3_q));  // open: out0, en
  not not_14 (not_14_out, decoder_3_out3);
  or or_5 (or_5_out, T2_Int_Out, decoder_3_out1);
  or or_6 (or_6_out, decoder_3_out2, j_k_ff_2_q);
  and and_14 (and_14_out, or_6_out, CLK_R);
  and and_15 (and_15_out, not_14_out, decoder_3_out3);
  J_K_Flip_Flop j_k_ff_2 (.Q(j_k_ff_2_q), .preset(and_15_out), .reset(T2_Int_Out));  // open: J, K, clk, Qn
  Counter #(.max('hffffffff), .width(32)) counter_2 (
    .clr(and_16_out), .up(1'b1), .clk(and_14_out), .Q(counter_2_q));  // open: load, count, D, carry
  and and_16 (and_16_out, or_5_out, CLK_F);
  assign xor_2_out = {register_2_q, register_1_q} ^ counter_2_q;  // XOR_Gate xor_2, 32 bits wide
  nor nor_5 (nor_5_out, xor_2_out[0], xor_2_out[1], xor_2_out[2], xor_2_out[3], xor_2_out[4], xor_2_out[5], xor_2_out[6], xor_2_out[7]);
  nor nor_6 (nor_6_out, xor_2_out[24], xor_2_out[25], xor_2_out[26], xor_2_out[27], xor_2_out[28], xor_2_out[29], xor_2_out[30], xor_2_out[31]);
  and and_17 (and_17_out, nor_5_out, nor_7_out);
  nor nor_7 (nor_7_out, xor_2_out[8], xor_2_out[9], xor_2_out[10], xor_2_out[11], xor_2_out[12], xor_2_out[13], xor_2_out[14], xor_2_out[15]);
  nor nor_8 (nor_8_out, xor_2_out[16], xor_2_out[17], xor_2_out[18], xor_2_out[19], xor_2_out[20], xor_2_out[21], xor_2_out[22], xor_2_out[23]);
  and and_18 (and_18_out, nor_8_out, nor_6_out);
  and and_19 (T2_Int_Out, and_17_out, and_18_out);
endmodule

module ActivationModule (
  input  [3:0] PatternR,
  input  [6:0] RE1,
  input  Diasble_R,
  input  [15:0] To_Bus,
  input  [6:0] RE2,
  input  Disable_W,
  input  [15:0] BUS1_In,
  input  [15:0] BUS2_In,
  input  [3:0] PatternW,
  input  [6:0] WE1,
  input  CLK_F,
  input  [6:0] WE2,
  input  CLK_R,
  output [2:0] Mode_R,
  output RE,
  output [15:0] BUS1_Out,
  output [15:0] BUS2_Out,
  output [2:0] Mode_W,
  output [15:0] from_Bus,
  output WE,
  output WE_F,
  output WE_R
);

  wire and_1_out, and_2_out, and_3_out, and_4_out, nor_1_out, nor_2_out, nor_3_out, nor_4_out, not_1_out,
       not_2_out, not_3_out, not_4_out, or_1_out, or_2_out, or_3_out, or_4_out, or_5_out, or_6_out, or_7_out,
       or_8_out;
  wire [3:0] xor_1_out, xor_2_out, xor_3_out, xor_4_out;

  assign Mode_R = not_1_out ? RE1[2:0] : 3'bz;  // Controlled_Buffer controlled_buffer_1
  assign Mode_R = nor_1_out ? RE2[2:0] : 3'bz;  // Controlled_Buffer controlled_buffer_2
  assign Mode_W = not_2_out ? WE2[2:0] : 3'bz;  // Controlled_Buffer controlled_buffer_3
  assign Mode_W = nor_3_out ? WE1[2:0] : 3'bz;  // Controlled_Buffer controlled_buffer_4
  not not_1 (not_1_out, nor_1_out);
  assign xor_1_out = PatternR ^ RE1[6:3];  // XOR_Gate xor_1, 4 bits wide
  assign xor_2_out = PatternR ^ RE2[6:3];  // XOR_Gate xor_2, 4 bits wide
  not not_2 (not_2_out, nor_3_out);
  assign xor_3_out = PatternW ^ WE1[6:3];  // XOR_Gate xor_3, 4 bits wide
  assign xor_4_out = PatternW ^ WE2[6:3];  // XOR_Gate xor_4, 4 bits wide
  or or_1 (or_1_out, xor_1_out[1], or_2_out);
  or or_2 (or_2_out, xor_1_out[2], xor_1_out[3]);
  or or_3 (or_3_out, xor_2_out[1], or_4_out);
  or or_4 (or_4_out, xor_2_out[2], xor_2_out[3]);
  or or_5 (or_5_out, xor_3_out[1], or_6_out);
  or or_6 (or_6_out, xor_3_out[2], xor_3_out[3]);
  or or_7 (or_7_out, xor_4_out[1], or_8_out);
  or or_8 (or_8_out, xor_4_out[2], xor_4_out[3]);
  nor nor_1 (nor_1_out, xor_1_out[0], or_1_out);
  nor nor_2 (nor_2_out, xor_2_out[0], or_3_out);
  nor nor_3 (nor_3_out, xor_3_out[0], or_5_out);
  nor nor_4 (nor_4_out, xor_4_out[0], or_7_out);
  and and_1 (and_1_out, nor_1_out, not_3_out);
  and and_2 (and_2_out, nor_2_out, not_3_out);
  not not_3 (not_3_out, Diasble_R);
  not not_4 (not_4_out, Disable_W);
  xor xor_5 (WE, nor_3_out, nor_4_out);
  xor xor_6 (RE, nor_1_out, nor_2_out);
  and and_3 (and_3_out, not_4_out, nor_3_out);
  and and_4 (and_4_out, not_4_out, nor_4_out);
  and and_5 (WE_F, WE, CLK_F);
  and and_6 (WE_R, WE, CLK_R);
  assign BUS1_Out = and_1_out ? To_Bus : 16'bz;  // Controlled_Buffer controlled_buffer_5
  assign BUS2_Out = and_2_out ? To_Bus : 16'bz;  // Controlled_Buffer controlled_buffer_6
  assign from_Bus = and_3_out ? BUS1_In : 16'bz;  // Controlled_Buffer controlled_buffer_7
  assign from_Bus = and_4_out ? BUS2_In : 16'bz;  // Controlled_Buffer controlled_buffer_8
endmodule
