// Logisim project register_file.circ as structural Verilog: 2 circuits, main circuit main
module main (
  input  [15:0] D_In,
  input  WE,
  input  R_Sup,
  input  S_Sup,
  input  [2:0] D_Sel,
  input  [2:0] A_Sel,
  input  [2:0] B_Sel
);

  wire and_1_out, and_2_out, clock_1_out, not_1_out, not_2_out, not_3_out;
  wire [15:0] registerfile_1_a_out, registerfile_1_b_out, registerfile_1_flag_out, registerfile_1_ip_out;

  // Probe on registerfile_1_a_out
  // Probe on registerfile_1_b_out
  Registerfile registerfile_1 (
    .FLAG_Out(registerfile_1_flag_out), .IP_Out(registerfile_1_ip_out), .A_Out(registerfile_1_a_out),
    .B_Out(registerfile_1_b_out), .D_Sel(D_Sel), .A_Sel(A_Sel), .B_Sel(B_Sel), .S_Sup(S_Sup), .R_Sup(R_Sup),
    .D_In(D_In), .CLK_R(and_2_out), .CLK_F(and_1_out), .WE(WE));  // open: Sup_Out, ZERO_ONE
  // Probe on registerfile_1_flag_out
  // Probe on registerfile_1_ip_out
  and and_1 (and_1_out, not_1_out, not_2_out);
  and and_2 (and_2_out, clock_1_out, not_3_out);
  not not_1 (not_1_out, clock_1_out);
  not not_2 (not_2_out, not_1_out);
  not not_3 (not_3_out, clock_1_out);
  Clock clock_1 (.out(clock_1_out));
  // Digital_Oscilloscope #(.nState(8)) digital_oscilloscope_1: pin names not known; wires that end beside it: clock_1_out
endmodule

module Registerfile (
  input  S_Sup,
  input  R_Sup,
  input  [15:0] D_In,
  input  CLK_R,
  input  ZERO_ONE,
  input  CLK_F,
  input  WE,
  input  [2:0] D_Sel,
  input  [2:0] A_Sel,
  input  [2:0] B_Sel,
  output Sup_Out,
  output [15:0] FLAG_Out,
  output [15:0] IP_Out,
  output [15:0] A_Out,
  output [15:0] B_Out
);

  wire and_1_out, and_2_out, and_3_out, and_4_out, and_5_out, and_6_out, and_7_out, and_8_out, and_9_out,
       and_10_out, decoder_1_out0, decoder_1_out1, decoder_1_out2, decoder_1_out3, decoder_2_out0,
       decoder_2_out1, decoder_2_out2, decoder_2_out3, decoder_3_out0, decoder_3_out1, decoder_3_out2,
       decoder_3_out3, decoder_4_out0, decoder_4_out1, decoder_4_out2, decoder_4_out3, decoder_5_out0,
       decoder_5_out1, decoder_5_out2, decoder_5_out3, decoder_6_out0, decoder_6_out1, decoder_6_out2,
       decoder_6_out3, not_1_out, not_2_out, not_3_out, not_4_out, not_5_out, not_6_out, not_7_out,
       not_8_out, not_9_out, not_10_out, not_11_out;
  wire [7:0] register_1_q, register_1_q_2;
  wire [15:0] A_q, B_q, C_q, D_q, SP_q;

  not not_1 (not_1_out, D_Sel[2]);
  not not_2 (not_2_out, A_Sel[2]);
  not not_3 (not_3_out, B_Sel[2]);
  Register #(.trigger("high"), .width(16)) register_1 (
    .D(D_In), .clk(CLK_R), .Q({register_1_q_2, register_1_q}));  // open: en, clr
  not not_4 (not_4_out, decoder_1_out0);
  not not_5 (not_5_out, decoder_1_out1);
  not not_6 (not_6_out, decoder_1_out2);
  not not_7 (not_7_out, decoder_1_out3);
  Decoder #(.select(2)) decoder_1 (
    .out0(decoder_1_out0), .out1(decoder_1_out1), .out2(decoder_1_out2), .out3(decoder_1_out3),
    .sel(D_Sel[1:0]), .en(not_1_out));
  not not_8 (not_8_out, decoder_2_out0);
  not not_9 (not_9_out, decoder_2_out1);
  not not_10 (not_10_out, decoder_2_out2);
  not not_11 (not_11_out, decoder_2_out3);
  Decoder #(.select(2)) decoder_2 (
    .out0(decoder_2_out0), .out1(decoder_2_out1), .out2(decoder_2_out2), .out3(decoder_2_out3),
    .sel(D_Sel[1:0]), .en(D_Sel[2]));
  Decoder #(.select(2)) decoder_3 (
    .out0(decoder_3_out0), .out1(decoder_3_out1), .out2(decoder_3_out2), .out3(decoder_3_out3),
    .sel(A_Sel[1:0]), .en(not_2_out));
  Decoder #(.select(2)) decoder_4 (
    .out0(decoder_4_out0), .out1(decoder_4_out1), .out2(decoder_4_out2), .out3(decoder_4_out3),
    .sel(A_Sel[1:0]), .en(A_Sel[2]));
  Decoder #(.select(2)) decoder_5 (
    .out0(decoder_5_out0), .out1(decoder_5_out1), .out2(decoder_5_out2), .out3(decoder_5_out3),
    .sel(B_Sel[1:0]), .en(not_3_out));
  Decoder #(.select(2)) decoder_6 (
    .out0(decoder_6_out0), .out1(decoder_6_out1), .out2(decoder_6_out2), .out3(decoder_6_out3),
    .sel(B_Sel[1:0]), .en(B_Sel[2]));
  and and_1 (and_1_out, CLK_F, WE);
  Register #(.trigger("high"), .width(16)) IP (
    .D({register_1_q_2, register_1_q}), .clk(and_2_out), .Q(IP_Out));  // open: en, clr
  and and_2 (and_2_out, and_1_out, ~not_5_out);  // AND_Gate
  assign A_Out = decoder_3_out0 ? {{15{1'b0}}, ZERO_ONE} : 16'bz;  // Controlled_Buffer controlled_buffer_1
  assign B_Out = decoder_5_out0 ? {{15{1'b0}}, ZERO_ONE} : 16'bz;  // Controlled_Buffer controlled_buffer_2
  assign A_Out = decoder_3_out1 ? IP_Out : 16'bz;  // Controlled_Buffer controlled_buffer_3
  assign B_Out = decoder_5_out1 ? IP_Out : 16'bz;  // Controlled_Buffer controlled_buffer_4
  Register #(.trigger("high"), .width(16)) SP (
    .D({register_1_q_2, register_1_q}), .clk(and_3_out), .Q(SP_q));  // open: en, clr
  and and_3 (and_3_out, and_1_out, ~not_6_out);  // AND_Gate
  Register #(.trigger("high"), .width(16)) A (
    .D({register_1_q_2, register_1_q}), .clk(and_4_out), .Q(A_q));  // open: en, clr
  and and_4 (and_4_out, and_1_out, ~not_7_out);  // AND_Gate
  assign A_Out = decoder_3_out2 ? SP_q : 16'bz;  // Controlled_Buffer controlled_buffer_5
  assign B_Out = decoder_5_out2 ? SP_q : 16'bz;  // Controlled_Buffer controlled_buffer_6
  assign A_Out = decoder_3_out3 ? A_q : 16'bz;  // Controlled_Buffer controlled_buffer_7
  assign B_Out = decoder_5_out3 ? A_q : 16'bz;  // Controlled_Buffer controlled_buffer_8
  Register #(.trigger("high"), .width(16)) B (
    .D({register_1_q_2, register_1_q}), .clk(and_5_out), .Q(B_q));  // open: en, clr
  and and_5 (and_5_out, and_1_out, ~not_8_out);  // AND_Gate
  Register #(.trigger("high"), .width(16)) C (
    .D({register_1_q_2, register_1_q}), .clk(and_6_out), .Q(C_q));  // open: en, clr
  and and_6 (and_6_out, and_1_out, ~not_9_out);  // AND_Gate
  assign A_Out = decoder_4_out0 ? B_q : 16'bz;  // Controlled_Buffer controlled_buffer_9
  assign B_Out = decoder_6_out0 ? B_q : 16'bz;  // Controlled_Buffer controlled_buffer_10
  assign A_Out = decoder_4_out1 ? C_q : 16'bz;  // Controlled_Buffer controlled_buffer_11
  assign B_Out = decoder_6_out1 ? C_q : 16'bz;  // Controlled_Buffer controlled_buffer_12
  Register #(.trigger("high"), .width(16)) D (
    .D({register_1_q_2, register_1_q}), .clk(and_7_out), .Q(D_q));  // open: en, clr
  and and_7 (and_7_out, and_1_out, ~not_10_out);  // AND_Gate
  Register #(.trigger("high")) FLAG0 (.D(register_1_q), .clk(and_8_out), .Q(FLAG_Out[7:0]));  // open: en, clr
  and and_8 (and_8_out, and_1_out, ~not_11_out);  // AND_Gate
  assign A_Out = decoder_4_out2 ? D_q : 16'bz;  // Controlled_Buffer controlled_buffer_13
  assign B_Out = decoder_6_out2 ? D_q : 16'bz;  // Controlled_Buffer controlled_buffer_14
  assign A_Out = decoder_4_out3 ? FLAG_Out : 16'bz;  // Controlled_Buffer controlled_buffer_15
  assign B_Out = decoder_6_out3 ? FLAG_Out : 16'bz;  // Controlled_Buffer controlled_buffer_16
  Register #(.trigger("high"), .width(7)) FLAG1 (
    .D(register_1_q_2[6:0]), .clk(and_9_out), .Q(FLAG_Out[14:8]));  // open: en, clr
  and and_9 (and_9_out, and_1_out, and_10_out);
  and and_10 (and_10_out, ~not_11_out, FLAG_Out[15]);  // AND_Gate
  D_Flip_Flop #(.trigger("high")) Sup (
    .D(register_1_q_2[7]), .clk(and_9_out), .Q(FLAG_Out[15]), .preset(S_Sup), .reset(R_Sup));  // open: Qn

  assign Sup_Out = FLAG_Out[15];
endmodule
