# Fritzing sketch not-gate (saved by Fritzing 0.9.3b)
circuit board: 2.80987cm x 1.69751cm
breadboards: 1

parts:
  Q1 = NPN-Transistor [package="TO92 [THT]"]
  R1 = Resistor [tolerance=±5% resistance=220 package=THT]
  S1 = Pushbutton [package="[THT]"]
  LED1 = LED - 5mm [color="Red (633nm)" package="5 mm [THT]"]
  R2 = Resistor [tolerance=±5% resistance=220 package=THT]
  J1 = female pin header, 2 pins [form="♀ (female)"]

nets (from the schematic view):
  GND: Q1.E, LED1.cathode, J1.pin2
  N1: Q1.B, R1.Pin_0
  N2: Q1.C, LED1.anode, R2.Pin_0
  N3: R1.Pin_1, S1.Pin_3, S1.Pin_4
  N4: S1.Pin_1, S1.Pin_2, R2.Pin_1, J1.pin1

notes:
  Sample
