// Logisim project Comperator.circ as structural Verilog: 1 circuit, main circuit main
module main (
  input  [3:0] in_1,
  input  [3:0] in_2,
  output out_3,
  output out_4
);

  wire and_3_out, and_4_out, and_5_out, and_6_out, and_7_out, and_8_out, and_9_out, and_10_out, and_11_out,
       and_12_out, and_13_out, not_3_out, not_4_out, not_5_out, or_3_out, or_4_out;
  wire [3:0] and_1_out, and_2_out, not_1_out, not_2_out, xor_1_out;

  assign not_1_out = ~in_1;  // NOT_Gate not_1, 4 bits wide
  assign not_2_out = ~in_2;  // NOT_Gate not_2, 4 bits wide
  assign xor_1_out = and_2_out ^ and_1_out;  // XOR_Gate xor_1, 4 bits wide
  assign and_1_out = in_2 & not_1_out;  // AND_Gate and_1, 4 bits wide
  assign and_2_out = not_2_out & in_1;  // AND_Gate and_2, 4 bits wide
  or or_1 (out_3, and_3_out, and_6_out, and_9_out, and_13_out);
  or or_2 (out_4, and_4_out, and_7_out, and_10_out, and_12_out);
  and and_3 (and_3_out, and_2_out[3], xor_1_out[3]);
  and and_4 (and_4_out, and_1_out[3], xor_1_out[3]);
  or or_3 (or_3_out, xor_1_out[2], xor_1_out[3]);
  not not_3 (not_3_out, xor_1_out[3]);
  and and_5 (and_5_out, not_3_out, xor_1_out[2]);
  and and_6 (and_6_out, and_2_out[2], and_5_out);
  and and_7 (and_7_out, and_1_out[2], and_5_out);
  or or_4 (or_4_out, xor_1_out[1], or_3_out);
  not not_4 (not_4_out, or_3_out);
  and and_8 (and_8_out, not_4_out, xor_1_out[1]);
  and and_9 (and_9_out, and_2_out[1], and_8_out);
  and and_10 (and_10_out, and_1_out[1], and_8_out);
  not not_5 (not_5_out, or_4_out);
  and and_11 (and_11_out, not_5_out, xor_1_out[0]);
  and and_12 (and_12_out, and_1_out[0], and_11_out);
  and and_13 (and_13_out, and_2_out[0], and_11_out);
endmodule
