// Logisim project Memory.circ as structural Verilog: 1 circuit, main circuit main
module main (
  input  [15:0] Page_Bound,
  input  [15:0] Page_Base,
  input  [15:0] Address,
  input  Disable_V_Memory,
  input  Write_Enable,
  input  Read_Enable,
  input  [15:0] Data_Input,
  output Error,
  output Ready,
  output [15:0] Data_Output
);

  wire and_1_out, and_2_out, and_3_out, and_4_out, and_5_out, and_6_out, and_7_out, and_8_out, buffer_1_out,
       clock_1_out, comparator_1_lt, not_1_out, not_2_out, not_3_out, not_4_out, not_5_out, not_6_out,
       or_1_out, or_2_out, or_3_out, or_4_out, t_ff_1_q;
  wire [7:0] ram_1_data, register_1_q;
  wire [15:0] adder_1_out, bit_extender_1_out, multiplexer_1_out, multiplexer_2_out;
  wire [15:8] ram_1_data_2;

  Clock clock_1 (.out(clock_1_out));
  not not_1 (not_1_out, Read_Enable);
  // Probe on Page_Bound
  // Probe on Page_Base
  // Probe on Address
  and and_1 (and_1_out, Write_Enable, not_1_out);
  not not_2 (not_2_out, and_1_out);
  or or_1 (or_1_out, and_1_out, and_2_out);
  and and_2 (and_2_out, not_2_out, Read_Enable);
  Comparator #(.width(16), .mode("unsigned")) comparator_1 (
    .a(Page_Bound), .b(bit_extender_1_out), .lt(comparator_1_lt));  // open: gt, eq
  Adder #(.width(16)) adder_1 (.a(Page_Base), .b(bit_extender_1_out), .out(adder_1_out));  // open: cin, cout
  assign bit_extender_1_out = {{8{1'b0}}, Address[15:8]};  // Bit_Extender bit_extender_1
  Register #(.trigger("low")) register_1 (.D(ram_1_data), .Q(register_1_q), .clk(t_ff_1_q));  // open: en, clr
  T_Flip_Flop t_ff_1 (.clk(clock_1_out), .T(or_1_out), .Q(t_ff_1_q), .reset(Disable_V_Memory));  // open: Qn, preset, en
  not not_3 (not_3_out, comparator_1_lt);
  or or_2 (or_2_out, not_3_out, Disable_V_Memory);
  Multiplexer #(.width(16)) multiplexer_1 (
    .in0(adder_1_out), .in1({register_1_q, Address[7:0]}), .out(multiplexer_1_out), .sel(and_3_out));  // open: en
  and and_3 (and_3_out, t_ff_1_q, not_4_out);
  not not_4 (not_4_out, Disable_V_Memory);
  or or_3 (or_3_out, Disable_V_Memory, and_3_out);
  and and_4 (and_4_out, or_2_out, and_1_out);
  and and_5 (and_5_out, or_2_out, and_2_out);
  // Probe on multiplexer_2_out
  Multiplexer #(.width(16)) multiplexer_2 (
    .in0(multiplexer_1_out), .in1(Address), .out(multiplexer_2_out), .sel(Disable_V_Memory));  // open: en
  not not_5 (not_5_out, and_3_out);
  and and_6 (and_6_out, or_3_out, and_4_out);
  and and_7 (and_7_out, or_3_out, and_5_out);
  // Probe on Data_Input
  or or_4 (or_4_out, not_5_out, and_7_out);
  RAM #(.addrWidth(16), .dataWidth(16), .bus("separate")) ram_1 (
    .addr(multiplexer_2_out), .din(Data_Input), .data({ram_1_data_2, ram_1_data}), .str(and_6_out),
    .sel(1'b1), .clk(clock_1_out), .ld(or_4_out));  // open: clr
  // Probe on {ram_1_data_2, ram_1_data}
  Register #(.width(16)) register_2 (
    .D({ram_1_data_2, ram_1_data}), .Q(Data_Output), .clk(buffer_1_out));  // open: en, clr
  buf buffer_1 (buffer_1_out, and_8_out);
  and and_8 (and_8_out, and_7_out, clock_1_out);
  and and_9 (Error, comparator_1_lt, not_6_out);
  not not_6 (not_6_out, Disable_V_Memory);
  or or_5 (Ready, and_6_out, and_7_out);
endmodule
