# Fritzing sketch Memory (saved by Fritzing 0.9.3b)
breadboards: 2

parts:
  Power_plug1 = Power plug
  IC1 = DIP - 28 pins [chip_label=SRAM package="DIP (Dual Inline) [THT]"]
  IC2 = DIP - 28 pins [chip_label=SRAM package="DIP (Dual Inline) [THT]"]
  IC3 = DIP - 20 pins [chip_label=Buffer package="DIP (Dual Inline) [THT]"]
  IC4 = DIP - 20 pins [chip_label=Buffer package="DIP (Dual Inline) [THT]"]
  IC5 = DIP - 20 pins [chip_label=Buffer package="DIP (Dual Inline) [THT]"]
  IC6 = DIP - 20 pins [chip_label=Buffer package="DIP (Dual Inline) [THT]"]
  J2 = female pin header, 8 pins [form="♀ (female)" part_number="Data I/O"]
  J1 = single row smd female pin header, 8 pins [form="♀ (female)" part_number="Address Input"]
  IC7 = DIP - 14 pins [chip_label=NAND package="DIP (Dual Inline) [THT]"]
  J3 = female pin header, 1 pin [form="♀ (female)" part_number=Clock]
  J4 = female pin header, 1 pin [form="♀ (female)" part_number="Write Enable"]
  J5 = female pin header, 1 pin [form="♀ (female)" part_number="Read Enable"]
  IC8 = DIP - 14 pins [chip_label=NAND package="DIP (Dual Inline) [THT]"]
  IC9 = DIP - 14 pins [chip_label=NAND package="DIP (Dual Inline) [THT]"]
  IC10 = DIP - 14 pins [chip_label=NAND package="DIP (Dual Inline) [THT]"]

nets:
  GND: Power_plug1.GND, IC1.A12, IC1.A7, IC1.GND, IC1.!CE, IC1.A10, IC1.A11, IC1.A9, IC1.A8, IC2.A12, IC2.A7, IC2.GND, IC2.!CE, IC2.A10, IC2.A11, IC2.A9, IC2.A8, IC3.GND, IC4.GND, IC5.GND, IC6.GND, IC7.GND, IC8.GND, IC9.GND, IC10.GND
  VCC: Power_plug1.VCC, IC1.CE2, IC1.Vcc, IC2.CE2, IC2.Vcc, IC3.Vcc, IC4.Vcc, IC5.Vcc, IC6.Vcc, IC7.VDD, IC8.VDD, IC9.VDD, IC10.VDD
  N1: IC1.A6, IC2.A6, J1.pin8
  N2: IC1.A5, IC2.A5, J1.pin7
  N3: IC1.A4, IC2.A4, J1.pin6
  N4: IC1.A3, IC2.A3, J1.pin5
  N5: IC1.A2, IC2.A2, J1.pin4
  N6: IC1.A1, IC2.A1, J1.pin3
  N7: IC1.A0, IC2.A0, J1.pin2
  N8: IC1.I/O1, IC3.A1, IC4.Y8
  N9: IC1.I/O2, IC3.A2, IC4.Y7
  N10: IC1.I/O3, IC3.A3, IC4.Y6
  N11: IC1.I/O4, IC3.A4, IC4.Y5
  N12: IC1.I/O5, IC3.A5, IC4.Y4
  N13: IC1.I/O6, IC3.A6, IC4.Y3
  N14: IC1.I/O7, IC3.A7, IC4.Y2
  N15: IC1.I/O8, IC3.A8, IC4.Y1
  N16: IC1.!OE, IC2.!OE, J4.pin1, IC8.F, IC10.C, IC10.D
  N17: IC1.!WE, IC8.K
  N18: IC2.I/O1, IC5.A1, IC6.Y8
  N19: IC2.I/O2, IC5.A2, IC6.Y7
  N20: IC2.I/O3, IC5.A3, IC6.Y6
  N21: IC2.I/O4, IC5.A4, IC6.Y5
  N22: IC2.I/O5, IC5.A5, IC6.Y4
  N23: IC2.I/O6, IC5.A6, IC6.Y3
  N24: IC2.I/O7, IC5.A7, IC6.Y2
  N25: IC2.I/O8, IC5.A8, IC6.Y1
  N26: IC2.!WE, IC8.J
  N27: IC3.!G1, IC5.!G1, IC10.J
  N28: IC3.Y8, IC4.A1, IC5.Y8, IC6.A1, J2.pin8
  N29: IC3.Y7, IC4.A2, IC5.Y7, IC6.A2, J2.pin7
  N30: IC3.Y6, IC4.A3, IC5.Y6, IC6.A3, J2.pin6
  N31: IC3.Y5, IC4.A4, IC5.Y5, IC6.A4, J2.pin5
  N32: IC3.Y4, IC4.A5, IC5.Y4, IC6.A5, J2.pin4
  N33: IC3.Y3, IC4.A6, IC5.Y3, IC6.A6, J2.pin3
  N34: IC3.Y2, IC4.A7, IC5.Y2, IC6.A7, J2.pin2
  N35: IC3.Y1, IC4.A8, IC5.Y1, IC6.A8, J2.pin1
  N36: IC3.!G2, IC4.!G1, J1.pin1, IC8.D, IC9.C, IC9.D
  N37: IC4.!G2, IC6.!G2, IC10.K
  N38: IC5.!G2, IC6.!G1, IC8.B, IC9.K
  N39: IC7.K, IC8.E
  N40: IC7.C, IC7.D, IC7.L
  N41: IC7.E, IC7.G, IC7.H, J3.pin1
  N42: IC7.F, IC7.M
  N43: J5.pin1, IC10.A, IC10.B
  N44: IC8.A, IC8.C, IC8.M
  N45: IC8.L, IC8.G, IC8.H

custom parts:
  DIP - 28 pins: A DIP stand-in part for whatever IC you want. With 28 pins on a 600mil dual inline package (DIP) footprint.
  DIP - 20 pins: A DIP stand-in part for whatever IC you want. With 20 pins on a 300mil dual inline package (DIP) footprint.
  DIP - 14 pins: A DIP stand-in part for whatever IC you want. With 14 pins on a 300mil dual inline package (DIP) footprint.
