// Logisim project suptraction.circ as structural Verilog: 1 circuit, main circuit main
module main (
  input  [3:0] in_1,
  input  [3:0] in_2
);

  wire [3:0] adder_1_out, adder_2_out, not_1_out;

  // Probe on in_1
  // Probe on in_2
  assign not_1_out = ~in_2;  // NOT_Gate not_1, 4 bits wide
  Adder #(.width(4)) adder_1 (.a(in_1), .b(not_1_out), .out(adder_1_out));  // open: cin, cout
  Adder #(.width(4)) adder_2 (.a(adder_1_out), .b(4'b0001), .out(adder_2_out));  // open: cin, cout
  // Probe on adder_2_out
endmodule
