# Fritzing sketch Untitled Sketch 2 (saved by Fritzing 0.9.3b)
breadboards: 2

parts:
  Power_plug1 = Power plug
  IC1 = DIP - 28 pins [chip_label=SRAM package="DIP (Dual Inline) [THT]"]
  IC2 = DIP - 28 pins [chip_label=SRAM package="DIP (Dual Inline) [THT]"]
  IC3 = DIP - 20 pins [chip_label=Buffer package="DIP (Dual Inline) [THT]"]
  IC4 = DIP - 20 pins [chip_label=Buffer package="DIP (Dual Inline) [THT]"]
  IC5 = DIP - 20 pins [chip_label=Buffer package="DIP (Dual Inline) [THT]"]
  IC6 = DIP - 20 pins [chip_label=Buffer package="DIP (Dual Inline) [THT]"]

nets:
  GND: Power_plug1.GND, IC1.GND, IC2.GND, IC3.!G1, IC3.GND, IC4.GND, IC4.!G2, IC5.GND, IC6.GND
  VCC: Power_plug1.VCC, IC1.Vcc, IC2.Vcc, IC3.Vcc, IC4.Vcc, IC5.Vcc, IC6.Vcc
  N1: IC1.I/O1, IC3.A1, IC4.Y8
  N2: IC1.I/O2, IC3.A2, IC4.Y7
  N3: IC1.I/O3, IC3.A3, IC4.Y6
  N4: IC1.I/O4, IC3.A4, IC4.Y5
  N5: IC1.I/O5, IC3.A5, IC4.Y4
  N6: IC1.I/O6, IC3.A6, IC4.Y3
  N7: IC1.I/O7, IC3.A7, IC4.Y2
  N8: IC1.I/O8, IC3.A8, IC4.Y1
  N9: IC2.I/O1, IC5.A1, IC6.Y8
  N10: IC2.I/O2, IC5.A2, IC6.Y7
  N11: IC2.I/O3, IC5.A3, IC6.Y6
  N12: IC2.I/O4, IC5.A4, IC6.Y5
  N13: IC2.I/O5, IC5.A5, IC6.Y4
  N14: IC2.I/O6, IC5.A6, IC6.Y3
  N15: IC2.I/O7, IC5.A7, IC6.Y2
  N16: IC2.I/O8, IC5.A8, IC6.Y1

custom parts:
  DIP - 28 pins: A DIP stand-in part for whatever IC you want. With 28 pins on a 600mil dual inline package (DIP) footprint.
  DIP - 20 pins: A DIP stand-in part for whatever IC you want. With 20 pins on a 300mil dual inline package (DIP) footprint.
