// Logisim project prototype.circ as structural Verilog: 1 circuit, main circuit main
module main (
  input  in_1,
  input  in_2,
  input  [3:0] in_3
);

  wire clock_1_out, d_ff_1_q, d_ff_2_q, d_ff_3_q, d_ff_4_q, d_ff_5_q, d_ff_6_q, d_ff_7_q, d_ff_8_q, d_ff_9_q,
       decoder_1_out1, decoder_1_out2, decoder_1_out3, decoder_1_out4, decoder_1_out5, decoder_1_out6,
       decoder_1_out7, decoder_1_out8, decoder_1_out9, decoder_2_out1, decoder_2_out2, keyboard_1_avail,
       not_1_out, not_2_out, or_1_out, pull_resistor_1_node, undriven, undriven_2;
  wire [3:0] pull_resistor_2_node, pull_resistor_3_node, pull_resistor_3_node_2;
  wire [6:0] controlled_buffer_1_out, keyboard_1_data;
  wire [7:0] adder_1_out, controlled_buffer_9_out, eax_q, ebx_q, eip_s_q, ram_1_data, subtractor_1_out,
       xor_1_out;
  wire [7:7] controlled_buffer_1_out_2;

  TTY tty_1 (.data(controlled_buffer_1_out), .clk(d_ff_2_q), .clr(pull_resistor_1_node));  // open: we
  Pull_Resistor pull_resistor_1 (.node(pull_resistor_1_node));
  Clock clock_1 (.out(clock_1_out));
  Keyboard #(.buflen(16)) keyboard_1 (
    .clk(not_1_out), .clr(or_1_out), .avail(keyboard_1_avail), .data(keyboard_1_data));  // open: re
  not not_1 (not_1_out, d_ff_1_q);
  or or_1 (or_1_out, in_1, pull_resistor_1_node);
  Decoder #(.select(4)) decoder_1 (
    .out1(decoder_1_out1), .out2(decoder_1_out2), .out3(decoder_1_out3), .out4(decoder_1_out4),
    .out5(decoder_1_out5), .out6(decoder_1_out6), .out7(decoder_1_out7), .out8(decoder_1_out8),
    .out9(decoder_1_out9), .sel(pull_resistor_2_node));  // open: out0, out10, out11, out12, out13, out14, out15, en
  Pull_Resistor pull_resistor_2 (.node(pull_resistor_2_node));
  D_Flip_Flop d_ff_1 (
    .clk(decoder_1_out2), .D(undriven), .Q(d_ff_1_q), .reset(pull_resistor_3_node[3]));  // open: Qn, preset, en
  D_Flip_Flop d_ff_2 (
    .clk(decoder_1_out1), .D(undriven), .Q(d_ff_2_q), .reset(pull_resistor_3_node[3]));  // open: Qn, preset, en
  Register eax (
    .D({controlled_buffer_1_out_2[7], controlled_buffer_1_out}), .Q(eax_q), .clk(d_ff_3_q),
    .clr(pull_resistor_1_node));  // open: en
  assign {controlled_buffer_1_out_2[7], controlled_buffer_1_out} = d_ff_1_q ? {1'b0, keyboard_1_data} : 8'bz;  // Controlled_Buffer controlled_buffer_1
  D_Flip_Flop d_ff_3 (
    .clk(decoder_1_out3), .D(undriven), .Q(d_ff_3_q), .reset(pull_resistor_3_node[3]));  // open: Qn, preset, en
  assign {controlled_buffer_1_out_2[7], controlled_buffer_1_out} = d_ff_4_q ? eax_q : 8'bz;  // Controlled_Buffer controlled_buffer_2
  D_Flip_Flop d_ff_4 (
    .clk(decoder_1_out4), .D(undriven), .Q(d_ff_4_q), .reset(pull_resistor_3_node[3]));  // open: Qn, preset, en
  Counter eip_s (
    .D(controlled_buffer_9_out), .count(controlled_buffer_9_out[0]), .Q(eip_s_q), .clk(clock_1_out),
    .clr(pull_resistor_1_node));  // open: load, carry
  Adder adder_1 (.a(eax_q), .b(ebx_q), .out(adder_1_out));  // open: cin, cout
  assign {controlled_buffer_1_out_2[7], controlled_buffer_1_out} = d_ff_7_q ? adder_1_out : 8'bz;  // Controlled_Buffer controlled_buffer_3
  Subtractor subtractor_1 (.a(eax_q), .b(ebx_q), .out(subtractor_1_out));  // open: bin, bout
  assign {controlled_buffer_1_out_2[7], controlled_buffer_1_out} = d_ff_6_q ? subtractor_1_out : 8'bz;  // Controlled_Buffer controlled_buffer_4
  assign xor_1_out = eax_q ^ ebx_q;  // XOR_Gate xor_1, 8 bits wide
  assign {controlled_buffer_1_out_2[7], controlled_buffer_1_out} = d_ff_5_q ? xor_1_out : 8'bz;  // Controlled_Buffer controlled_buffer_5
  D_Flip_Flop d_ff_5 (
    .clk(decoder_1_out5), .D(undriven), .Q(d_ff_5_q), .reset(pull_resistor_3_node[3]));  // open: Qn, preset, en
  D_Flip_Flop d_ff_6 (.clk(decoder_1_out6), .D(undriven), .Q(d_ff_6_q));  // open: Qn, preset, en, reset
  Register ebx (
    .D({controlled_buffer_1_out_2[7], controlled_buffer_1_out}), .Q(ebx_q), .clk(d_ff_8_q),
    .clr(pull_resistor_1_node));  // open: en
  D_Flip_Flop d_ff_7 (
    .clk(decoder_1_out7), .D(undriven), .Q(d_ff_7_q), .reset(pull_resistor_3_node[3]));  // open: Qn, preset, en
  assign pull_resistor_2_node = decoder_2_out1 ? pull_resistor_3_node_2 : 4'bz;  // Controlled_Buffer controlled_buffer_6
  RAM ram_1 (.addr(eip_s_q), .data(ram_1_data));  // open: sel, clk, ld, clr
  assign {controlled_buffer_1_out_2[7], controlled_buffer_1_out} = d_ff_9_q ? ebx_q : 8'bz;  // Controlled_Buffer controlled_buffer_7
  D_Flip_Flop d_ff_8 (
    .clk(decoder_1_out8), .D(undriven), .Q(d_ff_8_q), .reset(pull_resistor_3_node[3]));  // open: Qn, preset, en
  or or_2 (pull_resistor_1_node, in_2, decoder_2_out2);
  Decoder #(.select(4)) decoder_2 (
    .out1(decoder_2_out1), .out2(decoder_2_out2), .sel(pull_resistor_3_node));  // open: out0, out3, out4, out5, out6, out7, out8, out9, out10, out11, out12, out13, out14, out15, en
  Pull_Resistor pull_resistor_3 (.node({pull_resistor_3_node_2, pull_resistor_3_node}));
  assign {pull_resistor_3_node_2, pull_resistor_3_node} = not_2_out ? ram_1_data : 8'bz;  // Controlled_Buffer controlled_buffer_8
  not not_2 (not_2_out, undriven_2);
  assign controlled_buffer_9_out = undriven_2 ? ram_1_data : 8'bz;  // Controlled_Buffer controlled_buffer_9
  D_Flip_Flop d_ff_9 (
    .clk(decoder_1_out9), .D(undriven), .Q(d_ff_9_q), .reset(pull_resistor_3_node[3]));  // open: Qn, preset, en
  Decoder #(.select(4)) decoder_3 (.sel(in_3));  // open: out0, out1, out2, out3, out4, out5, out6, out7, out8, out9, out10, out11, out12, out13, out14, out15, en
  // Pins of 1 and 8 bits meet at controlled_buffer_9_out
endmodule
